// Logisim project Circ.circ as structural Verilog: 16 circuits, main circuit CPU
module Desk (
  input  in_1
);

  wire clock_1_out, keyboard_1_avail, not_1_out;
  wire [6:0] keyboard_1_data;

  Clock clock_1 (.out(clock_1_out));
  Controlled_Buffer controlled_buffer_1 (.in(clock_1_out), .en(keyboard_1_avail));  // open: out
  not not_1 (not_1_out, in_1);
  ControlPanel controlpanel_1 (.INPUT_BUS({1'b0, keyboard_1_data}), .ON_OFF(in_1), .RESET(not_1_out));
  Keyboard #(.buflen(1), .trigger("falling")) keyboard_1 (
    .avail(keyboard_1_avail), .data(keyboard_1_data));  // open: clk, re, clr
endmodule

module ControlPanel (
  input  RESET,
  input  ON_OFF,
  input  [7:0] INPUT_BUS
);

  wire clock_1_out;
  wire [7:0] cpu_1_data_output;
  wire [11:0] cpu_1_pm_address;
  wire [15:0] rom_1_data;

  Hex_Digit_Display hex_digit_display_1 (.value(INPUT_BUS[7:4]));  // open: dp
  Hex_Digit_Display hex_digit_display_2 (.value(INPUT_BUS[3:0]));  // open: dp
  ROM #(.addrWidth(12), .dataWidth(16)) rom_1 (.addr(cpu_1_pm_address), .data(rom_1_data));
  LED led_1 (.in(cpu_1_data_output[7]));
  CPU cpu_1 (
    .PM_DATA(rom_1_data), .DATA_INPUT(INPUT_BUS), .ENABLE(ON_OFF), .RESET(RESET),
    .PM_ADDRESS(cpu_1_pm_address), .DATA_OUTPUT(cpu_1_data_output));
  LED led_2 (.in(cpu_1_data_output[6]));
  LED led_3 (.in(cpu_1_data_output[5]));
  LED led_4 (.in(cpu_1_data_output[4]));
  LED led_5 (.in(cpu_1_data_output[3]));
  LED led_6 (.in(cpu_1_data_output[2]));
  LED led_7 (.in(cpu_1_data_output[1]));
  LED led_8 (.in(cpu_1_data_output[0]));
  TTY #(.cols(16), .rows(4)) tty_1 (.data(cpu_1_data_output[6:0]), .clk(clock_1_out), .clr(RESET));  // open: we
  Clock clock_1 (.out(clock_1_out));
  ROM #(.addrWidth(12), .dataWidth(16)) rom_2 ();  // open: addr, data

  // Notes on the sheet:
  //   contents of rom_1 (hex, n*v repeats v):
  //   713d 7404 7301 713d 8100 1230 4240 5009 3004 7138 8100 7130 8100 7130 8100 7120 8100 712d 8100 7120
  //   8100 714f 8100 7153 8100 7404 7301 7200 713d 8100 1230 4240 5022 301c 710a 8100 7176 8100 7130 8100
  //   712e 8100 7131 8100 710a 8100 710a 8100 713e 8100 7401 7355 7100 9100 3038 7242 4120 5044 1240 4230
  //   503e 3032 710a 4120 5035 8100 7200 3035 8100 3032
  //   contents of rom_2 (hex, n*v repeats v):
  //   713d 7404 7301 713d 8100 1230 4240 5009 3004 7138 8100 7130 8100 7130 8100 7120 8100 712d 8100 7120
  //   8100 714f 8100 7153 8100 7404 7301 7200 713d 8100 1230 4240 5022 301c 710a 8100 7176 8100 7130 8100
  //   712e 8100 7131 8100 710a 8100 710a 8100 713e 8100 7401 7355 7100 9100 3038 7242 4120 5044 1240 4230
  //   503e 3032 710a 4120 5035 8100 7200 3035 8100 3032
endmodule

module Disk (
  input  [6:0] Command
);
endmodule

module CPU (
  input  [15:0] PM_DATA,
  input  ENABLE,
  input  RESET,
  input  [7:0] DATA_INPUT,
  output [11:0] PM_ADDRESS,
  output [7:0] DATA_OUTPUT
);

  wire adder_1_cout, and_1_out, and_2_out, and_5_out, clock_1_out, clock_2_out, cmp_1_equals, CMPI,
       DEC_ERROR, DEC_NEGATIVE, DECI, decoder_1_out0, decoder_3_out1, decoder_3_out2, decoder_3_out3,
       decoder_3_out4, INBI, INC_ERROR, INCI, JE_STOP_ADD, JEI, JMPI, JMPN_STOP_ADD, JMPNI, LMEMI,
       MEM_UPDATE, MEMI, not_1_out, or_1_out, or_3_out, or_4_out, OUTBI, SETI;
  wire [3:0] DEC_UPDATE_REG, INB_UPDATE_REG, INC_UPDATE_REG, LMEM_UPDATE_REG, or_6_out, SET_UPDATE_REG;
  wire [7:0] AOUT, BOUT, COUT, DEC_EQUALS, DOUT, INB_REG_A, INB_REG_B, INB_REG_C, INB_REG_D, INC_EQUALS,
       LMEM_ADDRESS, LMEM_REG_A, LMEM_REG_B, LMEM_REG_C, LMEM_REG_D, MEM_ADDRESS, MEM_DATA, or_5_out,
       or_7_out, or_8_out, or_9_out, or_10_out, RAM_DATA_OUT, SET_REG_A, SET_REG_B, SET_REG_C, SET_REG_D;
  wire [11:0] adder_1_out, and_3_out, JE_PC_INPUT, JMP_PC_INPUT, JMPN_PC_INPUT, or_2_out;
  wire [11:11] not_2_out;

  Decoder #(.select(4)) decoder_1 (
    .out0(decoder_1_out0), .sel(PM_DATA[15:12]));  // open: out1, out2, out3, out4, out5, out6, out7, out8, out9, out10, out11, out12, out13, out14, out15, en
  or or_1 (or_1_out, decoder_1_out0, adder_1_cout);
  and and_1 (and_1_out, or_1_out, ENABLE);
  LED IDLE (.in(and_1_out));
  Decoder #(.select(4)) decoder_2 (
    .out1(INCI), .out2(DECI), .out3(JMPI), .out4(CMPI), .out5(JEI), .out6(JMPNI), .out7(SETI), .out8(OUTBI),
    .out9(INBI), .out10(MEMI), .out11(LMEMI), .sel(PM_DATA[15:12]));  // open: out0, out12, out13, out14, out15, en
  and and_2 (and_2_out, ENABLE, not_1_out);
  not not_1 (not_1_out, or_1_out);
  assign or_2_out = JE_PC_INPUT | JMP_PC_INPUT | JMPN_PC_INPUT | and_3_out;  // OR_Gate or_2, 12 bits wide
  assign and_3_out = adder_1_out & {12{not_2_out[11]}};  // AND_Gate and_3, 12 bits wide
  INC inc_1 (
    .ENABLE(INCI), .IDATA(PM_DATA[11:0]), .REG_A(AOUT), .REG_B(BOUT), .REG_C(COUT), .REG_D(DOUT),
    .ERROR(INC_ERROR), .EQUALS(INC_EQUALS), .UPDATE_REG(INC_UPDATE_REG));
  SET set_1 (
    .ENABLE(SETI), .IDATA(PM_DATA[11:0]), .REG_A(SET_REG_A), .REG_B(SET_REG_B), .REG_C(SET_REG_C),
    .REG_D(SET_REG_D), .UPDATE_REG(SET_UPDATE_REG));
  // AND_Gate and_4 has open pins: in0=ENABLE, in1=clock_1_out, out=open
  Register #(.width(12)) ProgramCounter (.D(or_2_out), .clk(and_5_out), .Q(PM_ADDRESS), .clr(RESET));  // open: en
  and and_5 (and_5_out, clock_1_out, and_2_out);
  not not_2 (not_2_out[11], or_3_out);
  or or_3 (or_3_out, JMPI, JE_STOP_ADD, JMPN_STOP_ADD);
  Clock clock_1 (.out(clock_1_out));
  buf or_4 (or_4_out, INC_ERROR);  // OR_Gate
  LED ERROR (.in(or_4_out));
  Adder #(.width(12)) adder_1 (.a(PM_ADDRESS), .b(12'h1), .out(adder_1_out), .cout(adder_1_cout));  // open: cin
  DEC dec_1 (
    .ENABLE(DECI), .IDATA(PM_DATA[11:0]), .REG_A(AOUT), .REG_B(BOUT), .REG_C(COUT), .REG_D(DOUT),
    .ERROR(DEC_ERROR), .EQUALS(DEC_EQUALS), .UPDATE_REG(DEC_UPDATE_REG));
  OUTB outb_1 (
    .ENABLE(OUTBI), .IDATA(PM_DATA[11:0]), .REG_A(AOUT), .REG_B(BOUT), .REG_C(COUT), .REG_D(DOUT),
    .CPU_OUT(DATA_OUTPUT));
  Clock clock_2 (.out(clock_2_out));
  RAM #(.clearpin("true"), .enables("line")) MAIN_RAM (
    .addr(or_5_out), .we(MEMI), .clk(clock_2_out), .din(MEM_DATA), .dout(RAM_DATA_OUT), .clr(RESET));
  assign or_5_out = MEM_ADDRESS | LMEM_ADDRESS;  // OR_Gate or_5, 8 bits wide
  JMPN jmpn_1 (
    .DEC_NEG(DEC_NEGATIVE), .ENABLE(JMPNI), .IDATA(PM_DATA[11:0]), .PC_REG(JMPN_PC_INPUT),
    .STOP_ADD(JMPN_STOP_ADD));
  JMP jmp_1 (.ENABLE(JMPI), .IDATA(PM_DATA[11:0]), .PC_REG(JMP_PC_INPUT));
  INB inb_1 (
    .ENABLE(INBI), .IDATA(PM_DATA[11:0]), .CPU_INPUT(DATA_INPUT), .REG_A(INB_REG_A), .REG_B(INB_REG_B),
    .REG_C(INB_REG_C), .REG_D(INB_REG_D), .UPDATE_REG(INB_UPDATE_REG));
  assign or_6_out = INC_UPDATE_REG | DEC_UPDATE_REG | SET_UPDATE_REG | INB_UPDATE_REG | LMEM_UPDATE_REG;  // OR_Gate or_6, 4 bits wide
  Decoder #(.select(4)) decoder_3 (
    .out1(decoder_3_out1), .out2(decoder_3_out2), .out3(decoder_3_out3), .out4(decoder_3_out4), .sel(or_6_out));  // open: out0, out5, out6, out7, out8, out9, out10, out11, out12, out13, out14, out15, en
  Register A (.D(or_7_out), .clk(decoder_3_out1), .Q(AOUT), .clr(RESET));  // open: en
  assign or_7_out = INC_EQUALS | DEC_EQUALS | SET_REG_A | INB_REG_A | LMEM_REG_A;  // OR_Gate or_7, 8 bits wide
  Register B (.D(or_8_out), .clk(decoder_3_out2), .Q(BOUT), .clr(RESET));  // open: en
  assign or_8_out = INC_EQUALS | DEC_EQUALS | SET_REG_B | INB_REG_B | LMEM_REG_B;  // OR_Gate or_8, 8 bits wide
  Register C (.D(or_9_out), .clk(decoder_3_out3), .Q(COUT), .clr(RESET));  // open: en
  assign or_9_out = INC_EQUALS | DEC_EQUALS | SET_REG_C | INB_REG_C | LMEM_REG_C;  // OR_Gate or_9, 8 bits wide
  Register D (.D(or_10_out), .clk(decoder_3_out4), .Q(DOUT), .clr(RESET));  // open: en
  assign or_10_out = INC_EQUALS | DEC_EQUALS | SET_REG_D | INB_REG_D | LMEM_REG_D;  // OR_Gate or_10, 8 bits wide
  CMP cmp_1 (
    .ENABLE(CMPI), .IDATA(PM_DATA[11:0]), .REG_A(AOUT), .REG_B(BOUT), .REG_C(COUT), .REG_D(DOUT),
    .EQUALS(cmp_1_equals));
  LMEM lmem_1 (
    .ENABLE(LMEMI), .IDATA(PM_DATA[11:0]), .RAM_DATA_IN(RAM_DATA_OUT), .RAM_ADDRESS(LMEM_ADDRESS),
    .REG_A(LMEM_REG_A), .REG_B(LMEM_REG_B), .REG_C(LMEM_REG_C), .REG_D(LMEM_REG_D),
    .UPDATE_REG(LMEM_UPDATE_REG));
  JE je_1 (.ENABLE(JEI), .CMP(cmp_1_equals), .IDATA(PM_DATA[11:0]), .PC_REG(JE_PC_INPUT), .STOP_ADD(JE_STOP_ADD));
  MEM mem_1 (
    .ENABLE(MEMI), .IDATA(PM_DATA[11:0]), .REG_A(AOUT), .REG_B(BOUT), .REG_C(COUT), .REG_D(DOUT),
    .RAM_UPDATE(MEM_UPDATE), .RAM_ADDRESS(MEM_ADDRESS), .RAM_DATA(MEM_DATA));

  // Other names for the same wires on the sheet: IDATA[11:0] = PM_DATA[11:0]

  // Notes on the sheet:
  //   Registers
endmodule

module ALU (
  input  ADDSUB,
  input  [7:0] INPUT2,
  input  [7:0] INPUT1,
  output OVERFLOW,
  output NEGATIVE,
  output [7:0] EQUALS
);

  wire adder_1_cout, subtractor_1_bout;
  wire [7:0] adder_1_out, and_1_out, and_2_out, subtractor_1_out;
  wire [7:7] not_1_out;

  not not_1 (not_1_out[7], ADDSUB);
  Adder adder_1 (.a(INPUT2), .b(INPUT1), .out(adder_1_out), .cout(adder_1_cout));  // open: cin
  Subtractor subtractor_1 (.a(INPUT1), .b(INPUT2), .out(subtractor_1_out), .bout(subtractor_1_bout));  // open: bin
  assign and_1_out = {8{ADDSUB}} & subtractor_1_out;  // AND_Gate and_1, 8 bits wide
  assign and_2_out = {8{not_1_out[7]}} & adder_1_out;  // AND_Gate and_2, 8 bits wide
  assign EQUALS = and_1_out | and_2_out;  // OR_Gate or_1, 8 bits wide
  or or_2 (OVERFLOW, adder_1_cout, subtractor_1_bout);
  and and_3 (NEGATIVE, subtractor_1_bout, ADDSUB);
endmodule

module INC (
  input  ENABLE,
  input  [11:0] IDATA,
  input  [7:0] REG_A,
  input  [7:0] REG_B,
  input  [7:0] REG_C,
  input  [7:0] REG_D,
  output ERROR,
  output [7:0] EQUALS,
  output [3:0] UPDATE_REG
);

  wire [3:3] or_3_out;
  wire [7:0] and_2_out, and_3_out, and_4_out, and_5_out, and_6_out, and_7_out, and_8_out, and_9_out,
       or_1_out, or_2_out;
  wire [7:7] decoder_1_out1, decoder_1_out2, decoder_1_out3, decoder_1_out4, decoder_2_out1, decoder_2_out2,
       decoder_2_out3, decoder_2_out4;
  wire [11:0] and_1_out;

  Decoder #(.select(4)) decoder_1 (
    .out1(decoder_1_out1[7]), .out2(decoder_1_out2[7]), .out3(decoder_1_out3[7]), .out4(decoder_1_out4[7]),
    .sel(and_1_out[11:8]));  // open: out0, out5, out6, out7, out8, out9, out10, out11, out12, out13, out14, out15, en
  assign and_1_out = {12{ENABLE}} & IDATA;  // AND_Gate and_1, 12 bits wide
  Decoder #(.select(4)) decoder_2 (
    .out1(decoder_2_out1[7]), .out2(decoder_2_out2[7]), .out3(decoder_2_out3[7]), .out4(decoder_2_out4[7]),
    .sel(and_1_out[7:4]));  // open: out0, out5, out6, out7, out8, out9, out10, out11, out12, out13, out14, out15, en
  assign and_2_out = {8{decoder_2_out1[7]}} & REG_A;  // AND_Gate and_2, 8 bits wide
  assign and_3_out = {8{decoder_2_out2[7]}} & REG_B;  // AND_Gate and_3, 8 bits wide
  assign and_4_out = {8{decoder_2_out3[7]}} & REG_C;  // AND_Gate and_4, 8 bits wide
  assign and_5_out = {8{decoder_2_out4[7]}} & REG_D;  // AND_Gate and_5, 8 bits wide
  assign and_6_out = {8{decoder_1_out1[7]}} & REG_A;  // AND_Gate and_6, 8 bits wide
  assign and_7_out = {8{decoder_1_out2[7]}} & REG_B;  // AND_Gate and_7, 8 bits wide
  assign and_8_out = {8{decoder_1_out3[7]}} & REG_C;  // AND_Gate and_8, 8 bits wide
  assign and_9_out = {8{decoder_1_out4[7]}} & REG_D;  // AND_Gate and_9, 8 bits wide
  assign or_1_out = and_6_out | and_7_out | and_8_out | and_9_out;  // OR_Gate or_1, 8 bits wide
  assign or_2_out = and_2_out | and_3_out | and_4_out | and_5_out;  // OR_Gate or_2, 8 bits wide
  ALU alu_1 (.ADDSUB(1'b0), .INPUT2(or_2_out), .INPUT1(or_1_out), .OVERFLOW(ERROR), .EQUALS(EQUALS));  // open: NEGATIVE
  or or_3 (or_3_out[3], EQUALS[0], EQUALS[1], EQUALS[2], EQUALS[3], EQUALS[4], EQUALS[5], EQUALS[6], EQUALS[7]);
  assign UPDATE_REG = {4{or_3_out[3]}} & and_1_out[11:8];  // AND_Gate and_10, 4 bits wide
endmodule

module DEC (
  input  ENABLE,
  input  [11:0] IDATA,
  input  [7:0] REG_A,
  input  [7:0] REG_B,
  input  [7:0] REG_C,
  input  [7:0] REG_D,
  output ERROR,
  output [7:0] EQUALS,
  output [3:0] UPDATE_REG
);

  wire [3:3] or_3_out;
  wire [7:0] and_2_out, and_3_out, and_4_out, and_5_out, and_6_out, and_7_out, and_8_out, and_9_out,
       or_1_out, or_2_out;
  wire [7:7] decoder_1_out1, decoder_1_out2, decoder_1_out3, decoder_1_out4, decoder_2_out1, decoder_2_out2,
       decoder_2_out3, decoder_2_out4;
  wire [11:0] and_1_out;

  Decoder #(.select(4)) decoder_1 (
    .out1(decoder_1_out1[7]), .out2(decoder_1_out2[7]), .out3(decoder_1_out3[7]), .out4(decoder_1_out4[7]),
    .sel(and_1_out[11:8]));  // open: out0, out5, out6, out7, out8, out9, out10, out11, out12, out13, out14, out15, en
  assign and_1_out = {12{ENABLE}} & IDATA;  // AND_Gate and_1, 12 bits wide
  Decoder #(.select(4)) decoder_2 (
    .out1(decoder_2_out1[7]), .out2(decoder_2_out2[7]), .out3(decoder_2_out3[7]), .out4(decoder_2_out4[7]),
    .sel(and_1_out[7:4]));  // open: out0, out5, out6, out7, out8, out9, out10, out11, out12, out13, out14, out15, en
  assign and_2_out = {8{decoder_2_out1[7]}} & REG_A;  // AND_Gate and_2, 8 bits wide
  assign and_3_out = {8{decoder_2_out2[7]}} & REG_B;  // AND_Gate and_3, 8 bits wide
  assign and_4_out = {8{decoder_2_out3[7]}} & REG_C;  // AND_Gate and_4, 8 bits wide
  assign and_5_out = {8{decoder_2_out4[7]}} & REG_D;  // AND_Gate and_5, 8 bits wide
  assign and_6_out = {8{decoder_1_out1[7]}} & REG_A;  // AND_Gate and_6, 8 bits wide
  assign and_7_out = {8{decoder_1_out2[7]}} & REG_B;  // AND_Gate and_7, 8 bits wide
  assign and_8_out = {8{decoder_1_out3[7]}} & REG_C;  // AND_Gate and_8, 8 bits wide
  assign and_9_out = {8{decoder_1_out4[7]}} & REG_D;  // AND_Gate and_9, 8 bits wide
  assign or_1_out = and_6_out | and_7_out | and_8_out | and_9_out;  // OR_Gate or_1, 8 bits wide
  assign or_2_out = and_2_out | and_3_out | and_4_out | and_5_out;  // OR_Gate or_2, 8 bits wide
  ALU alu_1 (.ADDSUB(1'b1), .INPUT2(or_2_out), .INPUT1(or_1_out), .OVERFLOW(ERROR), .EQUALS(EQUALS));  // open: NEGATIVE
  or or_3 (or_3_out[3], EQUALS[0], EQUALS[1], EQUALS[2], EQUALS[3], EQUALS[4], EQUALS[5], EQUALS[6], EQUALS[7]);
  assign UPDATE_REG = {4{or_3_out[3]}} & and_1_out[11:8];  // AND_Gate and_10, 4 bits wide
endmodule

module JMP (
  input  ENABLE,
  input  [11:0] IDATA,
  output [11:0] PC_REG
);

  and and_1 (PC_REG[11], IDATA[11], ENABLE);
  and and_2 (PC_REG[10], IDATA[10], ENABLE);
  and and_3 (PC_REG[9], IDATA[9], ENABLE);
  and and_4 (PC_REG[8], IDATA[8], ENABLE);
  and and_5 (PC_REG[7], IDATA[7], ENABLE);
  and and_6 (PC_REG[6], IDATA[6], ENABLE);
  and and_7 (PC_REG[5], IDATA[5], ENABLE);
  and and_8 (PC_REG[4], IDATA[4], ENABLE);
  and and_9 (PC_REG[3], IDATA[3], ENABLE);
  and and_10 (PC_REG[2], IDATA[2], ENABLE);
  and and_11 (PC_REG[1], IDATA[1], ENABLE);
  and and_12 (PC_REG[0], IDATA[0], ENABLE);
endmodule

module CMP (
  input  ENABLE,
  input  [11:0] IDATA,
  input  [7:0] REG_A,
  input  [7:0] REG_B,
  input  [7:0] REG_C,
  input  [7:0] REG_D,
  output EQUALS
);

  wire and_10_out, clock_1_out, xor_1_out, xor_2_out, xor_3_out, xor_4_out, xor_5_out, xor_6_out, xor_7_out,
       xor_8_out;
  wire [7:0] and_2_out, and_3_out, and_4_out, and_5_out, and_6_out, and_7_out, and_8_out, and_9_out,
       or_1_out, or_2_out;
  wire [7:7] decoder_1_out1, decoder_1_out2, decoder_1_out3, decoder_1_out4, decoder_2_out1, decoder_2_out2,
       decoder_2_out3, decoder_2_out4;
  wire [11:0] and_1_out;

  Decoder #(.select(4)) decoder_1 (
    .out1(decoder_1_out1[7]), .out2(decoder_1_out2[7]), .out3(decoder_1_out3[7]), .out4(decoder_1_out4[7]),
    .sel(and_1_out[11:8]));  // open: out0, out5, out6, out7, out8, out9, out10, out11, out12, out13, out14, out15, en
  assign and_1_out = {12{ENABLE}} & IDATA;  // AND_Gate and_1, 12 bits wide
  Decoder #(.select(4)) decoder_2 (
    .out1(decoder_2_out1[7]), .out2(decoder_2_out2[7]), .out3(decoder_2_out3[7]), .out4(decoder_2_out4[7]),
    .sel(and_1_out[7:4]));  // open: out0, out5, out6, out7, out8, out9, out10, out11, out12, out13, out14, out15, en
  assign and_2_out = {8{decoder_2_out1[7]}} & REG_A;  // AND_Gate and_2, 8 bits wide
  assign and_3_out = {8{decoder_2_out2[7]}} & REG_B;  // AND_Gate and_3, 8 bits wide
  assign and_4_out = {8{decoder_2_out3[7]}} & REG_C;  // AND_Gate and_4, 8 bits wide
  assign and_5_out = {8{decoder_2_out4[7]}} & REG_D;  // AND_Gate and_5, 8 bits wide
  assign and_6_out = {8{decoder_1_out1[7]}} & REG_A;  // AND_Gate and_6, 8 bits wide
  assign and_7_out = {8{decoder_1_out2[7]}} & REG_B;  // AND_Gate and_7, 8 bits wide
  assign and_8_out = {8{decoder_1_out3[7]}} & REG_C;  // AND_Gate and_8, 8 bits wide
  assign and_9_out = {8{decoder_1_out4[7]}} & REG_D;  // AND_Gate and_9, 8 bits wide
  assign or_1_out = and_6_out | and_7_out | and_8_out | and_9_out;  // OR_Gate or_1, 8 bits wide
  assign or_2_out = and_2_out | and_3_out | and_4_out | and_5_out;  // OR_Gate or_2, 8 bits wide
  xor xor_1 (xor_1_out, or_1_out[7], or_2_out[7]);
  xor xor_2 (xor_2_out, or_1_out[5], or_2_out[5]);
  xor xor_3 (xor_3_out, or_1_out[6], or_2_out[6]);
  xor xor_4 (xor_4_out, or_1_out[4], or_2_out[4]);
  xor xor_5 (xor_5_out, or_1_out[2], or_2_out[2]);
  xor xor_6 (xor_6_out, or_1_out[3], or_2_out[3]);
  xor xor_7 (xor_7_out, or_1_out[1], or_2_out[1]);
  xor xor_8 (xor_8_out, or_1_out[0], or_2_out[0]);
  Register #(.width(1)) register_1 (.D(and_10_out), .clk(clock_1_out), .Q(EQUALS));  // open: en, clr
  and and_10 (and_10_out, ~xor_8_out, ~xor_7_out, ~xor_5_out, ~xor_6_out, ~xor_4_out, ~xor_2_out, ~xor_3_out, ~xor_1_out);  // AND_Gate
  Clock clock_1 (.out(clock_1_out));
endmodule

module JE (
  input  ENABLE,
  input  CMP,
  input  [11:0] IDATA,
  output [11:0] PC_REG,
  output STOP_ADD
);

  and and_1 (STOP_ADD, ENABLE, CMP);
  and and_2 (PC_REG[11], IDATA[11], STOP_ADD);
  and and_3 (PC_REG[10], IDATA[10], STOP_ADD);
  and and_4 (PC_REG[9], IDATA[9], STOP_ADD);
  and and_5 (PC_REG[8], IDATA[8], STOP_ADD);
  and and_6 (PC_REG[7], IDATA[7], STOP_ADD);
  and and_7 (PC_REG[6], IDATA[6], STOP_ADD);
  and and_8 (PC_REG[5], IDATA[5], STOP_ADD);
  and and_9 (PC_REG[4], IDATA[4], STOP_ADD);
  and and_10 (PC_REG[3], IDATA[3], STOP_ADD);
  and and_11 (PC_REG[2], IDATA[2], STOP_ADD);
  and and_12 (PC_REG[1], IDATA[1], STOP_ADD);
  and and_13 (PC_REG[0], IDATA[0], STOP_ADD);
endmodule

module JMPN (
  input  DEC_NEG,
  input  ENABLE,
  input  [11:0] IDATA,
  output [11:0] PC_REG,
  output STOP_ADD
);

  and and_1 (STOP_ADD, ENABLE, DEC_NEG);
  and and_2 (PC_REG[11], IDATA[11], STOP_ADD);
  and and_3 (PC_REG[10], IDATA[10], STOP_ADD);
  and and_4 (PC_REG[9], IDATA[9], STOP_ADD);
  and and_5 (PC_REG[8], IDATA[8], STOP_ADD);
  and and_6 (PC_REG[7], IDATA[7], STOP_ADD);
  and and_7 (PC_REG[6], IDATA[6], STOP_ADD);
  and and_8 (PC_REG[5], IDATA[5], STOP_ADD);
  and and_9 (PC_REG[4], IDATA[4], STOP_ADD);
  and and_10 (PC_REG[3], IDATA[3], STOP_ADD);
  and and_11 (PC_REG[2], IDATA[2], STOP_ADD);
  and and_12 (PC_REG[1], IDATA[1], STOP_ADD);
  and and_13 (PC_REG[0], IDATA[0], STOP_ADD);
endmodule

module SET (
  input  ENABLE,
  input  [11:0] IDATA,
  output [7:0] REG_A,
  output [7:0] REG_B,
  output [7:0] REG_C,
  output [7:0] REG_D,
  output [3:0] UPDATE_REG
);

  wire [3:3] or_2_out;
  wire [7:0] or_1_out;
  wire [7:7] decoder_1_out1, decoder_1_out2, decoder_1_out3, decoder_1_out4;
  wire [11:0] and_1_out;

  Decoder #(.select(4)) decoder_1 (
    .out1(decoder_1_out1[7]), .out2(decoder_1_out2[7]), .out3(decoder_1_out3[7]), .out4(decoder_1_out4[7]),
    .sel(and_1_out[11:8]));  // open: out0, out5, out6, out7, out8, out9, out10, out11, out12, out13, out14, out15, en
  assign and_1_out = {12{ENABLE}} & IDATA;  // AND_Gate and_1, 12 bits wide
  assign REG_A = {8{decoder_1_out1[7]}} & and_1_out[7:0];  // AND_Gate and_2, 8 bits wide
  assign REG_B = {8{decoder_1_out2[7]}} & and_1_out[7:0];  // AND_Gate and_3, 8 bits wide
  assign REG_C = {8{decoder_1_out3[7]}} & and_1_out[7:0];  // AND_Gate and_4, 8 bits wide
  assign REG_D = {8{decoder_1_out4[7]}} & and_1_out[7:0];  // AND_Gate and_5, 8 bits wide
  assign or_1_out = REG_A | REG_B | REG_C | REG_D;  // OR_Gate or_1, 8 bits wide
  or or_2 (or_2_out[3], ENABLE, or_1_out[0], or_1_out[1], or_1_out[2], or_1_out[3], or_1_out[4], or_1_out[5], or_1_out[6], or_1_out[7]);
  assign UPDATE_REG = {4{or_2_out[3]}} & and_1_out[11:8];  // AND_Gate and_6, 4 bits wide
endmodule

module OUTB (
  input  ENABLE,
  input  [11:0] IDATA,
  input  [7:0] REG_A,
  input  [7:0] REG_B,
  input  [7:0] REG_C,
  input  [7:0] REG_D,
  output [7:0] CPU_OUT
);

  wire [7:0] and_2_out, and_3_out, and_4_out, and_5_out;
  wire [7:7] decoder_1_out1, decoder_1_out2, decoder_1_out3, decoder_1_out4;
  wire [11:0] and_1_out;

  Decoder #(.select(4)) decoder_1 (
    .out1(decoder_1_out1[7]), .out2(decoder_1_out2[7]), .out3(decoder_1_out3[7]), .out4(decoder_1_out4[7]),
    .sel(and_1_out[11:8]));  // open: out0, out5, out6, out7, out8, out9, out10, out11, out12, out13, out14, out15, en
  assign and_1_out = {12{ENABLE}} & IDATA;  // AND_Gate and_1, 12 bits wide
  assign and_2_out = {8{decoder_1_out1[7]}} & REG_A;  // AND_Gate and_2, 8 bits wide
  assign and_3_out = {8{decoder_1_out2[7]}} & REG_B;  // AND_Gate and_3, 8 bits wide
  assign and_4_out = {8{decoder_1_out3[7]}} & REG_C;  // AND_Gate and_4, 8 bits wide
  assign and_5_out = {8{decoder_1_out4[7]}} & REG_D;  // AND_Gate and_5, 8 bits wide
  assign CPU_OUT = and_2_out | and_3_out | and_4_out | and_5_out;  // OR_Gate or_1, 8 bits wide
endmodule

module INB (
  input  ENABLE,
  input  [11:0] IDATA,
  input  [7:0] CPU_INPUT,
  output [7:0] REG_A,
  output [7:0] REG_B,
  output [7:0] REG_C,
  output [7:0] REG_D,
  output [3:0] UPDATE_REG
);

  wire [3:3] or_2_out;
  wire [7:0] or_1_out;
  wire [7:7] decoder_1_out1, decoder_1_out2, decoder_1_out3, decoder_1_out4;
  wire [11:0] and_1_out;

  Decoder #(.select(4)) decoder_1 (
    .out1(decoder_1_out1[7]), .out2(decoder_1_out2[7]), .out3(decoder_1_out3[7]), .out4(decoder_1_out4[7]),
    .sel(and_1_out[11:8]));  // open: out0, out5, out6, out7, out8, out9, out10, out11, out12, out13, out14, out15, en
  assign and_1_out = {12{ENABLE}} & IDATA;  // AND_Gate and_1, 12 bits wide
  assign REG_A = {8{decoder_1_out1[7]}} & CPU_INPUT;  // AND_Gate and_2, 8 bits wide
  assign REG_B = {8{decoder_1_out2[7]}} & CPU_INPUT;  // AND_Gate and_3, 8 bits wide
  assign REG_C = {8{decoder_1_out3[7]}} & CPU_INPUT;  // AND_Gate and_4, 8 bits wide
  assign REG_D = {8{decoder_1_out4[7]}} & CPU_INPUT;  // AND_Gate and_5, 8 bits wide
  assign or_1_out = REG_A | REG_B | REG_C | REG_D;  // OR_Gate or_1, 8 bits wide
  or or_2 (or_2_out[3], or_1_out[0], or_1_out[1], or_1_out[2], or_1_out[3], or_1_out[4], or_1_out[5], or_1_out[6], or_1_out[7]);
  assign UPDATE_REG = {4{or_2_out[3]}} & and_1_out[11:8];  // AND_Gate and_6, 4 bits wide
endmodule

module MEM (
  input  ENABLE,
  input  [11:0] IDATA,
  input  [7:0] REG_A,
  input  [7:0] REG_B,
  input  [7:0] REG_C,
  input  [7:0] REG_D,
  output RAM_UPDATE,
  output [7:0] RAM_ADDRESS,
  output [7:0] RAM_DATA
);

  wire [7:0] and_2_out, and_3_out, and_4_out, and_5_out;
  wire [7:7] decoder_1_out1, decoder_1_out2, decoder_1_out3, decoder_1_out4;
  wire [11:8] and_1_out;

  Decoder #(.select(4)) decoder_1 (
    .out1(decoder_1_out1[7]), .out2(decoder_1_out2[7]), .out3(decoder_1_out3[7]), .out4(decoder_1_out4[7]),
    .sel(and_1_out));  // open: out0, out5, out6, out7, out8, out9, out10, out11, out12, out13, out14, out15, en
  assign {and_1_out, RAM_ADDRESS} = {12{ENABLE}} & IDATA;  // AND_Gate and_1, 12 bits wide
  assign and_2_out = {8{decoder_1_out1[7]}} & REG_A;  // AND_Gate and_2, 8 bits wide
  assign and_3_out = {8{decoder_1_out2[7]}} & REG_B;  // AND_Gate and_3, 8 bits wide
  assign and_4_out = {8{decoder_1_out3[7]}} & REG_C;  // AND_Gate and_4, 8 bits wide
  assign and_5_out = {8{decoder_1_out4[7]}} & REG_D;  // AND_Gate and_5, 8 bits wide
  assign RAM_DATA = and_2_out | and_3_out | and_4_out | and_5_out;  // OR_Gate or_1, 8 bits wide

  assign RAM_UPDATE = ENABLE;
endmodule

module LMEM (
  input  ENABLE,
  input  [11:0] IDATA,
  input  [7:0] RAM_DATA_IN,
  output [7:0] RAM_ADDRESS,
  output [7:0] REG_A,
  output [7:0] REG_B,
  output [7:0] REG_C,
  output [7:0] REG_D,
  output [3:0] UPDATE_REG
);

  wire [3:0] and_1_out;
  wire [3:3] or_2_out;
  wire [7:0] or_1_out;
  wire [7:7] decoder_1_out1, decoder_1_out2, decoder_1_out3, decoder_1_out4;

  Decoder #(.select(4)) decoder_1 (
    .out1(decoder_1_out1[7]), .out2(decoder_1_out2[7]), .out3(decoder_1_out3[7]), .out4(decoder_1_out4[7]),
    .sel(and_1_out));  // open: out0, out5, out6, out7, out8, out9, out10, out11, out12, out13, out14, out15, en
  assign {RAM_ADDRESS, and_1_out} = {12{ENABLE}} & IDATA;  // AND_Gate and_1, 12 bits wide
  assign REG_A = {8{decoder_1_out1[7]}} & RAM_DATA_IN;  // AND_Gate and_2, 8 bits wide
  assign REG_B = {8{decoder_1_out2[7]}} & RAM_DATA_IN;  // AND_Gate and_3, 8 bits wide
  assign REG_C = {8{decoder_1_out3[7]}} & RAM_DATA_IN;  // AND_Gate and_4, 8 bits wide
  assign REG_D = {8{decoder_1_out4[7]}} & RAM_DATA_IN;  // AND_Gate and_5, 8 bits wide
  assign or_1_out = REG_A | REG_B | REG_C | REG_D;  // OR_Gate or_1, 8 bits wide
  or or_2 (or_2_out[3], or_1_out[0], or_1_out[1], or_1_out[2], or_1_out[3], or_1_out[4], or_1_out[5], or_1_out[6], or_1_out[7]);
  assign UPDATE_REG = {4{or_2_out[3]}} & and_1_out;  // AND_Gate and_6, 4 bits wide
endmodule
