// Logisim project Circuit.circ as structural Verilog: 15 circuits, main circuit CPU
module ALU (
  input  in_1,
  input  in_2,
  input  in_3,
  input  in_4,
  input  INPUT_2,
  input  in_6,
  input  in_7,
  input  in_8,
  input  in_9,
  input  in_10,
  input  in_11,
  input  in_12,
  input  in_13,
  input  in_14,
  input  in_15,
  input  in_16,
  input  in_17,
  output OUT1,
  output OUT2,
  output OUT3,
  output OUT4,
  output OUT5,
  output OUT6,
  output OUT7,
  output OUT8,
  output Overflow,
  output NEGATIVE,
  output Zero
);

  wire adder_1_cout, adder_1_out, adder_2_cout, adder_2_out, adder_3_cout, adder_3_out, adder_4_cout,
       adder_4_out, adder_5_cout, adder_5_out, adder_6_cout, adder_6_out, adder_7_cout, adder_7_out,
       adder_8_cout, adder_8_out, and_1_out, and_2_out, and_3_out, and_4_out, and_5_out, and_6_out,
       and_7_out, and_8_out, and_9_out, and_10_out, and_11_out, and_12_out, and_13_out, and_14_out,
       and_15_out, and_16_out, and_17_out, and_18_out, and_19_out, and_20_out, and_21_out, and_22_out,
       and_23_out, and_24_out, and_25_out, and_26_out, and_27_out, and_28_out, and_29_out, and_30_out,
       and_31_out, and_32_out, and_34_out, and_35_out, not_1_out, not_2_out, not_3_out, not_4_out, or_1_out,
       or_2_out, or_11_out, subtractor_1_bout, subtractor_1_out, subtractor_2_bout, subtractor_2_out,
       subtractor_3_bout, subtractor_3_out, subtractor_4_bout, subtractor_4_out, subtractor_5_bout,
       subtractor_5_out, subtractor_6_bout, subtractor_6_out, subtractor_7_bout, subtractor_7_out,
       subtractor_8_bout, subtractor_8_out;

  not not_1 (not_1_out, in_1);
  not not_2 (not_2_out, not_1_out);
  and and_1 (and_1_out, in_17, not_1_out);
  and and_2 (and_2_out, in_9, not_1_out);
  and and_3 (and_3_out, in_16, not_1_out);
  and and_4 (and_4_out, in_8, not_1_out);
  and and_5 (and_5_out, in_15, not_1_out);
  and and_6 (and_6_out, in_7, not_1_out);
  and and_7 (and_7_out, in_14, not_1_out);
  and and_8 (and_8_out, in_6, not_1_out);
  and and_9 (and_9_out, in_13, not_1_out);
  and and_10 (and_10_out, INPUT_2, not_1_out);
  and and_11 (and_11_out, in_12, not_1_out);
  and and_12 (and_12_out, in_4, not_1_out);
  and and_13 (and_13_out, in_11, not_1_out);
  and and_14 (and_14_out, in_3, not_1_out);
  and and_15 (and_15_out, in_10, not_1_out);
  and and_16 (and_16_out, in_2, not_1_out);
  and and_17 (and_17_out, in_17, not_2_out);
  and and_18 (and_18_out, in_9, not_2_out);
  and and_19 (and_19_out, in_16, not_2_out);
  and and_20 (and_20_out, in_8, not_2_out);
  and and_21 (and_21_out, in_15, not_2_out);
  and and_22 (and_22_out, in_7, not_2_out);
  and and_23 (and_23_out, in_14, not_2_out);
  and and_24 (and_24_out, in_6, not_2_out);
  and and_25 (and_25_out, in_13, not_2_out);
  and and_26 (and_26_out, INPUT_2, not_2_out);
  and and_27 (and_27_out, in_12, not_2_out);
  and and_28 (and_28_out, in_4, not_2_out);
  and and_29 (and_29_out, in_11, not_2_out);
  and and_30 (and_30_out, in_3, not_2_out);
  and and_31 (and_31_out, in_10, not_2_out);
  and and_32 (and_32_out, in_2, not_2_out);
  Adder #(.width(1)) adder_1 (.a(and_1_out), .b(and_2_out), .out(adder_1_out), .cout(adder_1_cout));  // open: cin
  Adder #(.width(1)) adder_2 (.a(and_3_out), .b(and_4_out), .out(adder_2_out), .cin(adder_1_cout), .cout(adder_2_cout));
  Adder #(.width(1)) adder_3 (.a(and_5_out), .b(and_6_out), .out(adder_3_out), .cin(adder_2_cout), .cout(adder_3_cout));
  Adder #(.width(1)) adder_4 (.a(and_7_out), .b(and_8_out), .out(adder_4_out), .cin(adder_3_cout), .cout(adder_4_cout));
  Adder #(.width(1)) adder_5 (
    .a(and_9_out), .b(and_10_out), .out(adder_5_out), .cin(adder_4_cout), .cout(adder_5_cout));
  Adder #(.width(1)) adder_6 (
    .a(and_11_out), .b(and_12_out), .out(adder_6_out), .cin(adder_5_cout), .cout(adder_6_cout));
  Adder #(.width(1)) adder_7 (
    .a(and_13_out), .b(and_14_out), .out(adder_7_out), .cin(adder_6_cout), .cout(adder_7_cout));
  Adder #(.width(1)) adder_8 (
    .a(and_15_out), .b(and_16_out), .out(adder_8_out), .cin(adder_7_cout), .cout(adder_8_cout));
  Subtractor #(.width(1)) subtractor_1 (
    .a(and_17_out), .b(and_18_out), .out(subtractor_1_out), .bout(subtractor_1_bout));  // open: bin
  Subtractor #(.width(1)) subtractor_2 (
    .a(and_19_out), .b(and_20_out), .out(subtractor_2_out), .bin(subtractor_1_bout), .bout(subtractor_2_bout));
  Subtractor #(.width(1)) subtractor_3 (
    .a(and_21_out), .b(and_22_out), .out(subtractor_3_out), .bin(subtractor_2_bout), .bout(subtractor_3_bout));
  Subtractor #(.width(1)) subtractor_4 (
    .a(and_23_out), .b(and_24_out), .out(subtractor_4_out), .bin(subtractor_3_bout), .bout(subtractor_4_bout));
  Subtractor #(.width(1)) subtractor_5 (
    .a(and_25_out), .b(and_26_out), .out(subtractor_5_out), .bin(subtractor_4_bout), .bout(subtractor_5_bout));
  Subtractor #(.width(1)) subtractor_6 (
    .a(and_27_out), .b(and_28_out), .out(subtractor_6_out), .bin(subtractor_5_bout), .bout(subtractor_6_bout));
  Subtractor #(.width(1)) subtractor_7 (
    .a(and_29_out), .b(and_30_out), .out(subtractor_7_out), .bin(subtractor_6_bout), .bout(subtractor_7_bout));
  Subtractor #(.width(1)) subtractor_8 (
    .a(and_31_out), .b(and_32_out), .out(subtractor_8_out), .bin(subtractor_7_bout), .bout(subtractor_8_bout));
  or or_1 (or_1_out, adder_8_out, adder_7_out, adder_6_out, adder_5_out, adder_4_out, adder_3_out, adder_2_out, adder_1_out);
  not not_3 (not_3_out, or_1_out);
  or or_2 (or_2_out, subtractor_8_out, subtractor_7_out, subtractor_6_out, subtractor_5_out, subtractor_4_out, subtractor_3_out, subtractor_2_out, subtractor_1_out);
  not not_4 (not_4_out, or_2_out);
  or or_3 (OUT1, adder_1_out, subtractor_1_out);
  or or_4 (OUT2, adder_2_out, subtractor_2_out);
  or or_5 (OUT3, adder_3_out, subtractor_3_out);
  or or_6 (OUT4, adder_4_out, subtractor_4_out);
  or or_7 (OUT5, adder_5_out, subtractor_5_out);
  or or_8 (OUT6, adder_6_out, subtractor_6_out);
  or or_9 (OUT7, adder_7_out, subtractor_7_out);
  or or_10 (OUT8, adder_8_out, subtractor_8_out);
  or or_11 (or_11_out, adder_8_cout, subtractor_8_bout);
  xor xor_1 (Overflow, or_11_out, not_2_out);
  and and_33 (NEGATIVE, not_2_out, subtractor_8_bout);
  and and_34 (and_34_out, not_3_out, not_1_out);
  or or_12 (Zero, and_34_out, and_35_out);
  and and_35 (and_35_out, not_4_out, not_2_out);

  // Notes on the sheet:
  //   ADD / SUB
  //   INPUT 1
  //   ALU
endmodule

module CPU (
  input  [7:0] in_1,
  input  ENABLE,
  output [7:0] out_3
);

  wire and_1_out, and_2_out, ci_1_out_5, ci_1_out_7, clock_1_out, CMP, cmp_1_out_7, INB, INC,
       inc_iar_1_out_4, JE, JMP, LMEM, MEM, mem_1_update_memory, not_1_out, or_1_out, or_3_out, OUTB, SET;
  wire [3:0] inb_1_update_register, inc_1_update_register, lmem_1_update_register, or_2_out,
       set_1_update_register;
  wire [7:0] AO, BIA, BIB, BIC, BID, BO, CO, DO, IA, IB, IC, ID, IIA, IIB, IIC, IID, inc_iar_1_out_3,
       INSTRUCTION_ADDRESS_REGISTER_q, je_1_instruction_address_register, jmp_1_instruction_address_register,
       lmem_1_memory_address, mem_1_memory_address, mem_1_memory_data, MIA, MIB, MIC, MID, or_4_out,
       or_5_out, or_10_out, ram_1_data, SIA, SIB, SIC, SID;
  wire [11:0] IDATA;
  wire [15:0] rom_1_data;
  wire [15:12] INSTRUCTION_REGISTER_q;

  INC inc_1 (
    .REGISTER_A(AO), .REGISTER_B(BO), .REGISTER_C(CO), .REGISTER_D(DO), .in_1(INC), .in_2(IDATA),
    .UPDATE_REGISTER(inc_1_update_register), .REGISTER_A_2(IIA), .REGISTER_B_2(IIB), .REGISTER_C_2(IIC),
    .REGISTER_D_2(IID));
  buf or_1 (or_1_out, inc_iar_1_out_4);  // OR_Gate
  LED ERROR (.in(or_1_out));
  LMEM lmem_1 (
    .MEMORY_DATA(ram_1_data), .MEMORY_ADDRESS(lmem_1_memory_address), .REGISTER_A(MIA), .REGISTER_B(MIB),
    .REGISTER_C(MIC), .REGISTER_D(MID), .in_1(LMEM), .in_2(IDATA), .UPDATE_REGISTER(lmem_1_update_register));
  INB inb_1 (
    .in_3(in_1), .out_4(BIA), .out_5(BIB), .out_6(BIC), .out_7(BID), .in_1(INB), .in_2(IDATA),
    .UPDATE_REGISTER(inb_1_update_register));
  assign or_2_out = inc_1_update_register | inb_1_update_register | lmem_1_update_register | set_1_update_register;  // OR_Gate or_2, 4 bits wide
  Register A (.D(IA), .Q(AO), .clk(or_2_out[3]));  // open: en, clr
  LED IDLE (.in(or_3_out));
  LED INSTRUCTION_ADDRESS_REGISTER_OVERFLOW (.in(inc_iar_1_out_4));
  Register B (.D(IB), .Q(BO), .clk(or_2_out[2]));  // open: en, clr
  not not_1 (not_1_out, or_3_out);
  or or_3 (or_3_out, inc_iar_1_out_4, ci_1_out_5);
  SET set_1 (
    .in_1(SET), .in_2(IDATA), .out_3(SIA), .out_4(SIB), .out_5(SIC), .out_6(SID),
    .UPDATE_REGISTER(set_1_update_register));
  Register C (.D(IC), .Q(CO), .clk(or_2_out[1]));  // open: en, clr
  CI ci_1 (
    .DECODER(INSTRUCTION_REGISTER_q[15]), .in_2(INSTRUCTION_REGISTER_q[14]),
    .in_3(INSTRUCTION_REGISTER_q[13]), .in_4(INSTRUCTION_REGISTER_q[12]), .out_5(ci_1_out_5), .out_6(INC),
    .out_7(ci_1_out_7), .out_8(JMP), .out_9(CMP), .out_10(JE), .out_11(SET), .out_12(OUTB), .out_13(INB),
    .out_14(MEM), .out_15(LMEM));
  Register D (.D(ID), .Q(DO), .clk(or_2_out[0]));  // open: en, clr
  Register #(.width(16)) INSTRUCTION_REGISTER (
    .D(rom_1_data), .Q({INSTRUCTION_REGISTER_q, IDATA}), .clk(and_2_out));  // open: en, clr
  Register INSTRUCTION_ADDRESS_REGISTER (
    .D(or_4_out), .Q(INSTRUCTION_ADDRESS_REGISTER_q), .clk(and_1_out));  // open: en, clr
  assign or_4_out = or_5_out | inc_iar_1_out_3;  // OR_Gate or_4, 8 bits wide
  and and_1 (and_1_out, ENABLE, not_1_out, clock_1_out);
  Clock clock_1 (.out(clock_1_out));
  JMP jmp_1 (.INSTRUCTION_ADDRESS_REGISTER(jmp_1_instruction_address_register), .in_1(JMP), .in_2(IDATA));
  and and_2 (and_2_out, clock_1_out, ENABLE);
  assign or_5_out = jmp_1_instruction_address_register | je_1_instruction_address_register;  // OR_Gate or_5, 8 bits wide
  assign IA = MIA | BIA | SIA | IIA;  // OR_Gate or_6, 8 bits wide
  OUTB outb_1 (.in_3(AO), .in_4(BO), .in_5(CO), .in_6(DO), .out_7(out_3), .in_1(OUTB), .in_2(IDATA));
  CMP cmp_1 (.in_3(AO), .in_4(BO), .in_5(CO), .in_6(DO), .out_7(cmp_1_out_7), .in_1(CMP), .in_2(IDATA));
  INC_IAR inc_iar_1 (
    .in_2(INSTRUCTION_ADDRESS_REGISTER_q), .out_3(inc_iar_1_out_3), .out_4(inc_iar_1_out_4), .in_1(JMP));
  assign IB = MIB | BIB | SIB | IIB;  // OR_Gate or_7, 8 bits wide
  JE je_1 (
    .INSTRUCTION_ADDRESS_REGISTER(je_1_instruction_address_register), .in_3(cmp_1_out_7), .in_1(IDATA),
    .in_2(JE));
  ROM #(.dataWidth(16)) rom_1 (.addr(INSTRUCTION_ADDRESS_REGISTER_q), .data(rom_1_data));  // open: sel
  assign IC = MIC | BIC | SIC | IIC;  // OR_Gate or_8, 8 bits wide
  MEM mem_1 (
    .in_3(AO), .in_4(BO), .in_5(CO), .in_6(DO), .MEMORY_ADDRESS(mem_1_memory_address),
    .MEMORY_DATA(mem_1_memory_data), .in_1(MEM), .in_2(IDATA), .UPDATE_MEMORY(mem_1_update_memory));
  assign ID = MID | BID | SID | IID;  // OR_Gate or_9, 8 bits wide
  assign or_10_out = mem_1_memory_address | lmem_1_memory_address;  // OR_Gate or_10, 8 bits wide
  RAM #(.bus("separate")) ram_1 (
    .addr(or_10_out), .din(mem_1_memory_data), .data(ram_1_data), .str(mem_1_update_memory),
    .clk(mem_1_update_memory));  // open: sel, ld, clr

  // Other names for the same wires on the sheet: OA[7:0] = AO; OB[7:0] = BO; OC[7:0] = CO; OD[7:0] = DO

  // Notes on the sheet:
  //   CPU
endmodule

module CI (
  input  DECODER,
  input  in_2,
  input  in_3,
  input  in_4,
  output out_5,
  output out_6,
  output out_7,
  output out_8,
  output out_9,
  output out_10,
  output out_11,
  output out_12,
  output out_13,
  output out_14,
  output out_15
);

  wire and_1_out, not_1_out, not_2_out, not_3_out, not_4_out, not_5_out, not_6_out, not_7_out, not_8_out,
       not_9_out, not_10_out, not_11_out, not_12_out, not_13_out, not_14_out, not_15_out, not_16_out,
       not_17_out, not_18_out, not_19_out, not_20_out, not_21_out, not_22_out, not_23_out, not_24_out,
       not_25_out, not_26_out, not_27_out;

  buf or_1 (out_5, and_1_out);  // OR_Gate
  not not_1 (not_1_out, in_3);
  not not_2 (not_2_out, in_2);
  not not_3 (not_3_out, DECODER);
  not not_4 (not_4_out, in_4);
  and and_1 (and_1_out, not_3_out, not_2_out, not_1_out, not_4_out);
  not not_5 (not_5_out, in_2);
  not not_6 (not_6_out, in_3);
  not not_7 (not_7_out, DECODER);
  and and_2 (out_6, not_7_out, not_5_out, not_6_out, in_4);
  not not_8 (not_8_out, in_4);
  not not_9 (not_9_out, DECODER);
  not not_10 (not_10_out, in_2);
  and and_3 (out_7, not_9_out, not_10_out, in_3, not_8_out);
  not not_11 (not_11_out, DECODER);
  not not_12 (not_12_out, in_2);
  and and_4 (out_8, not_11_out, not_12_out, in_3, in_4);
  not not_13 (not_13_out, DECODER);
  not not_14 (not_14_out, in_4);
  not not_15 (not_15_out, in_3);
  and and_5 (out_9, not_13_out, in_2, not_15_out, not_14_out);
  not not_16 (not_16_out, DECODER);
  not not_17 (not_17_out, in_3);
  and and_6 (out_10, not_16_out, in_2, not_17_out, in_4);
  not not_18 (not_18_out, DECODER);
  not not_19 (not_19_out, in_4);
  and and_7 (out_11, not_18_out, in_2, in_3, not_19_out);
  not not_20 (not_20_out, DECODER);
  and and_8 (out_12, not_20_out, in_2, in_3, in_4);
  not not_21 (not_21_out, in_3);
  not not_22 (not_22_out, in_4);
  not not_23 (not_23_out, in_2);
  and and_9 (out_13, DECODER, not_23_out, not_21_out, not_22_out);
  not not_24 (not_24_out, in_3);
  not not_25 (not_25_out, in_2);
  and and_10 (out_14, DECODER, not_25_out, not_24_out, in_4);
  not not_26 (not_26_out, in_2);
  not not_27 (not_27_out, in_4);
  and and_11 (out_15, DECODER, not_26_out, in_3, not_27_out);
endmodule

module JMP (
  input  in_1,
  input  [11:0] in_2,
  output [7:0] INSTRUCTION_ADDRESS_REGISTER
);

  and and_1 (INSTRUCTION_ADDRESS_REGISTER[7], in_1, in_2[11]);
  and and_2 (INSTRUCTION_ADDRESS_REGISTER[4], in_1, in_2[8]);
  and and_3 (INSTRUCTION_ADDRESS_REGISTER[5], in_1, in_2[9]);
  and and_4 (INSTRUCTION_ADDRESS_REGISTER[6], in_1, in_2[10]);
  and and_5 (INSTRUCTION_ADDRESS_REGISTER[3], in_1, in_2[7]);
  and and_6 (INSTRUCTION_ADDRESS_REGISTER[1], in_1, in_2[5]);
  and and_7 (INSTRUCTION_ADDRESS_REGISTER[2], in_1, in_2[6]);
  // AND_Gate and_8 has open pins: in0=in_1, in1=in_2[3], out=open
  and and_9 (INSTRUCTION_ADDRESS_REGISTER[0], in_1, in_2[4]);
  // AND_Gate and_10 has open pins: in0=in_1, in1=in_2[2], out=open
  // AND_Gate and_11 has open pins: in0=in_1, in1=in_2[0], out=open
  // AND_Gate and_12 has open pins: in0=in_1, in1=in_2[1], out=open

  // Notes on the sheet:
  //   JMP
endmodule

module SET (
  input  in_1,
  input  [11:0] in_2,
  output [7:0] out_3,
  output [7:0] out_4,
  output [7:0] out_5,
  output [7:0] out_6,
  output [3:0] UPDATE_REGISTER
);

  wire and_1_out, and_2_out, and_3_out, and_4_out, and_13_out, and_14_out, and_15_out, and_16_out,
       clock_1_out, not_1_out, not_2_out, not_3_out, not_4_out, not_5_out, not_6_out, not_7_out, not_8_out,
       not_9_out, not_10_out, not_11_out;
  wire [7:0] and_12_out;

  and and_1 (and_1_out, in_1, in_2[11]);
  and and_2 (and_2_out, in_1, in_2[8]);
  and and_3 (and_3_out, in_1, in_2[10]);
  and and_4 (and_4_out, in_1, in_2[9]);
  and and_5 (and_12_out[7], in_1, in_2[7]);
  and and_6 (and_12_out[6], in_1, in_2[6]);
  and and_7 (and_12_out[3], in_1, in_2[3]);
  and and_8 (and_12_out[4], in_1, in_2[4]);
  and and_9 (and_12_out[5], in_1, in_2[5]);
  and and_10 (and_12_out[2], in_1, in_2[2]);
  and and_11 (and_12_out[1], in_1, in_2[1]);
  and and_12 (and_12_out[0], in_1, in_2[0]);
  not not_1 (not_1_out, and_4_out);
  not not_2 (not_2_out, and_1_out);
  not not_3 (not_3_out, and_3_out);
  and and_13 (and_13_out, not_2_out, not_3_out, not_1_out, and_2_out);
  not not_4 (not_4_out, and_1_out);
  not not_5 (not_5_out, and_2_out);
  not not_6 (not_6_out, and_3_out);
  and and_14 (and_14_out, not_4_out, not_6_out, and_4_out, not_5_out);
  not not_7 (not_7_out, and_1_out);
  not not_8 (not_8_out, and_3_out);
  and and_15 (and_15_out, not_7_out, not_8_out, and_4_out, and_2_out);
  not not_9 (not_9_out, and_2_out);
  not not_10 (not_10_out, and_1_out);
  not not_11 (not_11_out, and_4_out);
  and and_16 (and_16_out, not_10_out, and_3_out, not_11_out, not_9_out);
  and and_17 (out_3[0], and_13_out, and_12_out[0]);
  and and_18 (out_3[1], and_13_out, and_12_out[1]);
  and and_19 (out_4[0], and_14_out, and_12_out[0]);
  and and_20 (out_4[1], and_14_out, and_12_out[1]);
  and and_21 (out_5[0], and_15_out, and_12_out[0]);
  and and_22 (out_5[1], and_15_out, and_12_out[1]);
  and and_23 (out_6[0], and_16_out, and_12_out[0]);
  and and_24 (out_6[1], and_16_out, and_12_out[1]);
  and and_25 (out_3[2], and_13_out, and_12_out[2]);
  and and_26 (out_3[3], and_13_out, and_12_out[3]);
  and and_27 (out_4[2], and_14_out, and_12_out[2]);
  and and_28 (out_4[3], and_14_out, and_12_out[3]);
  and and_29 (out_5[2], and_15_out, and_12_out[2]);
  and and_30 (out_5[3], and_15_out, and_12_out[3]);
  and and_31 (out_6[2], and_16_out, and_12_out[2]);
  and and_32 (out_6[3], and_16_out, and_12_out[3]);
  and and_33 (UPDATE_REGISTER[2], and_14_out, clock_1_out);
  and and_34 (UPDATE_REGISTER[3], and_13_out, clock_1_out);
  and and_35 (UPDATE_REGISTER[1], and_15_out, clock_1_out);
  and and_36 (out_3[4], and_13_out, and_12_out[4]);
  and and_37 (out_3[5], and_13_out, and_12_out[5]);
  and and_38 (out_4[4], and_14_out, and_12_out[4]);
  and and_39 (out_4[5], and_14_out, and_12_out[5]);
  and and_40 (out_5[4], and_15_out, and_12_out[4]);
  and and_41 (out_5[5], and_15_out, and_12_out[5]);
  and and_42 (out_6[4], and_16_out, and_12_out[4]);
  and and_43 (out_6[5], and_16_out, and_12_out[5]);
  and and_44 (UPDATE_REGISTER[0], and_16_out, clock_1_out);
  and and_45 (out_3[6], and_13_out, and_12_out[6]);
  and and_46 (out_4[6], and_14_out, and_12_out[6]);
  and and_47 (out_5[6], and_15_out, and_12_out[6]);
  and and_48 (out_6[6], and_16_out, and_12_out[6]);
  Clock clock_1 (.out(clock_1_out));
  and and_49 (out_3[7], and_13_out, and_12_out[7]);
  and and_50 (out_4[7], and_14_out, and_12_out[7]);
  and and_51 (out_5[7], and_15_out, and_12_out[7]);
  and and_52 (out_6[7], and_16_out, and_12_out[7]);

  // Notes on the sheet:
  //   SET
  //   First Register is A
  //   First Register is B
  //   First Register is C
  //   Second Register is D
endmodule

module ControlPanel (
  input  in_1,
  input  in_2,
  input  in_3,
  input  in_4,
  input  in_5,
  input  in_6,
  input  in_7,
  input  in_8,
  input  in_9
);

  wire [7:0] cpu_1_out_3;

  CPU cpu_1 (.in_1({in_9, in_8, in_7, in_6, in_5, in_4, in_3, in_2}), .out_3(cpu_1_out_3), .ENABLE(in_1));
  Hex_Digit_Display hex_digit_display_1 (.value(cpu_1_out_3[3:0]));  // open: dp
  Hex_Digit_Display hex_digit_display_2 (.value(cpu_1_out_3[7:4]));  // open: dp
endmodule

module INC_IAR (
  input  in_1,
  input  [7:0] in_2,
  output [7:0] out_3,
  output out_4
);

  wire not_1_out;
  wire [7:0] and_1_out;

  not not_1 (not_1_out, in_1);
  and and_1 (and_1_out[0], not_1_out, in_2[0]);
  and and_2 (and_1_out[1], not_1_out, in_2[1]);
  and and_3 (and_1_out[2], not_1_out, in_2[2]);
  and and_4 (and_1_out[3], not_1_out, in_2[3]);
  and and_5 (and_1_out[4], not_1_out, in_2[4]);
  and and_6 (and_1_out[5], not_1_out, in_2[5]);
  and and_7 (and_1_out[6], not_1_out, in_2[6]);
  and and_8 (and_1_out[7], not_1_out, in_2[7]);
  ALU alu_1 (
    .OUT1(out_3[0]), .OUT2(out_3[1]), .OUT3(out_3[2]), .OUT4(out_3[3]), .OUT5(out_3[4]), .OUT6(out_3[5]),
    .OUT7(out_3[6]), .OUT8(out_3[7]), .Overflow(out_4), .in_1(1'b0), .in_2(1'b0), .in_3(1'b0), .in_4(1'b0),
    .INPUT_2(1'b0), .in_6(1'b0), .in_7(1'b0), .in_8(1'b0), .in_9(1'b1), .in_10(and_1_out[7]),
    .in_11(and_1_out[6]), .in_12(and_1_out[5]), .in_13(and_1_out[4]), .in_14(and_1_out[3]),
    .in_15(and_1_out[2]), .in_16(and_1_out[1]), .in_17(and_1_out[0]));  // open: NEGATIVE, Zero

  // Notes on the sheet:
  //   INC_IAR
endmodule

module INB (
  input  in_1,
  input  [11:0] in_2,
  input  [7:0] in_3,
  output [7:0] out_4,
  output [7:0] out_5,
  output [7:0] out_6,
  output [7:0] out_7,
  output [3:0] UPDATE_REGISTER
);

  wire and_1_out, and_2_out, and_3_out, and_5_out, and_13_out, and_14_out, and_15_out, and_16_out,
       clock_1_out, not_1_out, not_2_out, not_3_out, not_4_out, not_5_out, not_6_out, not_7_out, not_8_out,
       not_9_out, not_10_out, not_11_out;
  wire [7:0] and_12_out;

  and and_1 (and_1_out, in_1, in_2[11]);
  and and_2 (and_2_out, in_1, in_2[9]);
  and and_3 (and_3_out, in_1, in_2[10]);
  and and_4 (and_12_out[7], in_1, in_2[7]);
  and and_5 (and_5_out, in_1, in_2[8]);
  and and_6 (and_12_out[6], in_1, in_2[6]);
  and and_7 (and_12_out[5], in_1, in_2[5]);
  and and_8 (and_12_out[4], in_1, in_2[4]);
  and and_9 (and_12_out[3], in_1, in_2[3]);
  and and_10 (and_12_out[2], in_1, in_2[2]);
  and and_11 (and_12_out[1], in_1, in_2[1]);
  and and_12 (and_12_out[0], in_1, in_2[0]);
  not not_1 (not_1_out, and_3_out);
  not not_2 (not_2_out, and_1_out);
  not not_3 (not_3_out, and_2_out);
  and and_13 (and_13_out, not_2_out, not_1_out, not_3_out, and_5_out);
  not not_4 (not_4_out, and_5_out);
  not not_5 (not_5_out, and_1_out);
  not not_6 (not_6_out, and_3_out);
  and and_14 (and_14_out, not_5_out, not_6_out, and_2_out, not_4_out);
  not not_7 (not_7_out, and_3_out);
  not not_8 (not_8_out, and_1_out);
  and and_15 (and_15_out, not_8_out, not_7_out, and_2_out, and_5_out);
  not not_9 (not_9_out, and_2_out);
  not not_10 (not_10_out, and_5_out);
  not not_11 (not_11_out, and_1_out);
  and and_16 (and_16_out, not_11_out, and_3_out, not_9_out, not_10_out);
  and and_17 (out_4[0], and_13_out, in_3[0]);
  and and_18 (out_4[1], and_13_out, in_3[1]);
  and and_19 (out_5[0], and_14_out, in_3[0]);
  and and_20 (out_5[1], and_14_out, in_3[1]);
  and and_21 (out_6[0], and_15_out, in_3[0]);
  and and_22 (out_6[1], and_15_out, in_3[1]);
  and and_23 (out_7[0], and_16_out, in_3[0]);
  and and_24 (out_7[1], and_16_out, in_3[1]);
  and and_25 (UPDATE_REGISTER[2], and_14_out, clock_1_out);
  and and_26 (UPDATE_REGISTER[3], and_13_out, clock_1_out);
  and and_27 (out_4[2], and_13_out, in_3[2]);
  and and_28 (out_4[3], and_13_out, in_3[3]);
  and and_29 (out_5[2], and_14_out, in_3[2]);
  and and_30 (out_5[3], and_14_out, in_3[3]);
  and and_31 (out_6[2], and_15_out, in_3[2]);
  and and_32 (out_6[3], and_15_out, in_3[3]);
  and and_33 (out_7[2], and_16_out, in_3[2]);
  and and_34 (out_7[3], and_16_out, in_3[3]);
  and and_35 (UPDATE_REGISTER[0], and_16_out, clock_1_out);
  and and_36 (UPDATE_REGISTER[1], and_15_out, clock_1_out);
  and and_37 (out_4[4], and_13_out, in_3[4]);
  and and_38 (out_4[5], and_13_out, in_3[5]);
  and and_39 (out_5[4], and_14_out, in_3[4]);
  and and_40 (out_5[5], and_14_out, in_3[5]);
  and and_41 (out_6[4], and_15_out, in_3[4]);
  and and_42 (out_6[5], and_15_out, in_3[5]);
  and and_43 (out_7[4], and_16_out, in_3[4]);
  and and_44 (out_7[5], and_16_out, in_3[5]);
  Clock clock_1 (.out(clock_1_out));
  and and_45 (out_4[6], and_13_out, in_3[6]);
  and and_46 (out_5[6], and_14_out, in_3[6]);
  and and_47 (out_6[6], and_15_out, in_3[6]);
  and and_48 (out_7[6], and_16_out, in_3[6]);
  and and_49 (out_4[7], and_13_out, in_3[7]);
  and and_50 (out_5[7], and_14_out, in_3[7]);
  and and_51 (out_6[7], and_15_out, in_3[7]);
  and and_52 (out_7[7], and_16_out, in_3[7]);

  // Notes on the sheet:
  //   INB
  //   First Register is A
  //   First Register is B
  //   First Register is C
  //   First Register is D
endmodule

module OUTB (
  input  in_1,
  input  [11:0] in_2,
  input  [7:0] in_3,
  input  [7:0] in_4,
  input  [7:0] in_5,
  input  [7:0] in_6,
  output [7:0] out_7
);

  wire and_1_out, and_2_out, and_3_out, and_5_out, and_13_out, and_14_out, and_15_out, and_16_out,
       and_49_out, clock_1_out, not_1_out, not_2_out, not_3_out, not_4_out, not_5_out, not_6_out, not_7_out,
       not_8_out, not_9_out, not_10_out, not_11_out, or_1_out;
  wire [7:0] and_12_out, and_17_out, and_19_out, and_21_out, and_23_out, or_2_out;

  and and_1 (and_1_out, in_1, in_2[10]);
  and and_2 (and_2_out, in_1, in_2[11]);
  and and_3 (and_3_out, in_1, in_2[9]);
  and and_4 (and_12_out[7], in_1, in_2[7]);
  and and_5 (and_5_out, in_1, in_2[8]);
  and and_6 (and_12_out[5], in_1, in_2[5]);
  and and_7 (and_12_out[6], in_1, in_2[6]);
  and and_8 (and_12_out[4], in_1, in_2[4]);
  and and_9 (and_12_out[1], in_1, in_2[1]);
  and and_10 (and_12_out[2], in_1, in_2[2]);
  and and_11 (and_12_out[3], in_1, in_2[3]);
  and and_12 (and_12_out[0], in_1, in_2[0]);
  not not_1 (not_1_out, and_3_out);
  not not_2 (not_2_out, and_2_out);
  not not_3 (not_3_out, and_1_out);
  and and_13 (and_13_out, not_2_out, not_3_out, not_1_out, and_5_out);
  not not_4 (not_4_out, and_1_out);
  not not_5 (not_5_out, and_2_out);
  not not_6 (not_6_out, and_5_out);
  and and_14 (and_14_out, not_5_out, not_4_out, and_3_out, not_6_out);
  not not_7 (not_7_out, and_1_out);
  not not_8 (not_8_out, and_2_out);
  and and_15 (and_15_out, not_8_out, not_7_out, and_3_out, and_5_out);
  not not_9 (not_9_out, and_5_out);
  not not_10 (not_10_out, and_2_out);
  not not_11 (not_11_out, and_3_out);
  and and_16 (and_16_out, not_10_out, and_1_out, not_11_out, not_9_out);
  and and_17 (and_17_out[0], and_13_out, in_3[0]);
  and and_18 (and_17_out[1], and_13_out, in_3[1]);
  and and_19 (and_19_out[0], and_14_out, in_4[0]);
  and and_20 (and_19_out[1], and_14_out, in_4[1]);
  and and_21 (and_21_out[0], and_15_out, in_5[0]);
  and and_22 (and_21_out[1], and_15_out, in_5[1]);
  and and_23 (and_23_out[0], and_16_out, in_6[0]);
  and and_24 (and_23_out[1], and_16_out, in_6[1]);
  or or_1 (or_1_out, and_13_out, and_14_out, and_15_out, and_16_out);
  and and_25 (and_17_out[2], and_13_out, in_3[2]);
  and and_26 (and_17_out[3], and_13_out, in_3[3]);
  and and_27 (and_19_out[2], and_14_out, in_4[2]);
  and and_28 (and_19_out[3], and_14_out, in_4[3]);
  and and_29 (and_21_out[2], and_15_out, in_5[2]);
  and and_30 (and_21_out[3], and_15_out, in_5[3]);
  and and_31 (and_23_out[2], and_16_out, in_6[2]);
  and and_32 (and_23_out[3], and_16_out, in_6[3]);
  and and_33 (and_17_out[4], and_13_out, in_3[4]);
  and and_34 (and_17_out[5], and_13_out, in_3[5]);
  and and_35 (and_19_out[4], and_14_out, in_4[4]);
  and and_36 (and_19_out[5], and_14_out, in_4[5]);
  and and_37 (and_21_out[4], and_15_out, in_5[4]);
  and and_38 (and_21_out[5], and_15_out, in_5[5]);
  and and_39 (and_23_out[4], and_16_out, in_6[4]);
  and and_40 (and_23_out[5], and_16_out, in_6[5]);
  and and_41 (and_17_out[6], and_13_out, in_3[6]);
  and and_42 (and_19_out[6], and_14_out, in_4[6]);
  and and_43 (and_21_out[6], and_15_out, in_5[6]);
  and and_44 (and_23_out[6], and_16_out, in_6[6]);
  and and_45 (and_17_out[7], and_13_out, in_3[7]);
  and and_46 (and_19_out[7], and_14_out, in_4[7]);
  and and_47 (and_21_out[7], and_15_out, in_5[7]);
  and and_48 (and_23_out[7], and_16_out, in_6[7]);
  assign or_2_out = and_17_out | and_19_out | and_21_out | and_23_out;  // OR_Gate or_2, 8 bits wide
  Register register_1 (.D(or_2_out), .Q(out_7), .clk(and_49_out));  // open: en, clr
  and and_49 (and_49_out, or_1_out, clock_1_out);
  Clock clock_1 (.out(clock_1_out));

  // Notes on the sheet:
  //   OUTB
  //   First Register is A
  //   First Register is B
  //   First Register is C
  //   Second Register is D
endmodule

module CMP (
  input  in_1,
  input  [11:0] in_2,
  input  [7:0] in_3,
  input  [7:0] in_4,
  input  [7:0] in_5,
  input  [7:0] in_6,
  output out_7
);

  wire and_1_out, and_2_out, and_3_out, and_4_out, and_5_out, and_6_out, and_7_out, and_8_out, and_21_out,
       and_22_out, and_23_out, and_24_out, and_41_out, and_42_out, and_43_out, and_44_out, and_85_out,
       and_86_out, clock_1_out, not_1_out, not_2_out, not_3_out, not_4_out, not_5_out, not_6_out, not_7_out,
       not_8_out, not_9_out, not_10_out, not_11_out, not_12_out, not_13_out, not_14_out, not_15_out,
       not_16_out, not_17_out, not_18_out, not_19_out, not_20_out, not_21_out, not_22_out, not_23_out,
       not_24_out, not_25_out, not_26_out, not_27_out, not_28_out, not_29_out, not_30_out, xor_1_out,
       xor_2_out, xor_3_out, xor_4_out, xor_5_out, xor_6_out, xor_7_out, xor_8_out;
  wire [3:0] and_20_out;
  wire [7:0] and_12_out, and_13_out, and_14_out, and_15_out, and_16_out, and_17_out, and_18_out, and_19_out,
       or_1_out, or_2_out;

  and and_1 (and_1_out, in_1, in_2[9]);
  and and_2 (and_2_out, in_1, in_2[10]);
  and and_3 (and_3_out, in_1, in_2[11]);
  and and_4 (and_4_out, in_1, in_2[7]);
  and and_5 (and_5_out, in_1, in_2[8]);
  and and_6 (and_6_out, in_1, in_2[4]);
  and and_7 (and_7_out, in_1, in_2[6]);
  and and_8 (and_8_out, in_1, in_2[5]);
  and and_9 (and_20_out[2], in_1, in_2[2]);
  and and_10 (and_20_out[1], in_1, in_2[1]);
  and and_11 (and_20_out[3], in_1, in_2[3]);
  and and_12 (and_12_out[0], and_21_out, in_3[0]);
  and and_13 (and_13_out[0], and_22_out, in_4[0]);
  and and_14 (and_14_out[0], and_23_out, in_5[0]);
  and and_15 (and_15_out[0], and_24_out, in_6[0]);
  and and_16 (and_16_out[0], and_41_out, in_3[0]);
  and and_17 (and_17_out[0], and_42_out, in_4[0]);
  and and_18 (and_18_out[0], and_43_out, in_5[0]);
  and and_19 (and_19_out[0], and_44_out, in_6[0]);
  and and_20 (and_20_out[0], in_1, in_2[0]);
  not not_1 (not_1_out, and_3_out);
  not not_2 (not_2_out, and_2_out);
  not not_3 (not_3_out, and_1_out);
  and and_21 (and_21_out, not_1_out, not_2_out, not_3_out, and_5_out);
  not not_4 (not_4_out, and_5_out);
  not not_5 (not_5_out, and_3_out);
  not not_6 (not_6_out, and_2_out);
  and and_22 (and_22_out, not_5_out, not_6_out, and_1_out, not_4_out);
  not not_7 (not_7_out, and_2_out);
  not not_8 (not_8_out, and_3_out);
  and and_23 (and_23_out, not_8_out, not_7_out, and_1_out, and_5_out);
  not not_9 (not_9_out, and_1_out);
  not not_10 (not_10_out, and_5_out);
  not not_11 (not_11_out, and_3_out);
  and and_24 (and_24_out, not_11_out, and_2_out, not_9_out, not_10_out);
  and and_25 (and_12_out[1], and_21_out, in_3[1]);
  and and_26 (and_12_out[2], and_21_out, in_3[2]);
  and and_27 (and_13_out[1], and_22_out, in_4[1]);
  and and_28 (and_13_out[2], and_22_out, in_4[2]);
  and and_29 (and_14_out[1], and_23_out, in_5[1]);
  and and_30 (and_14_out[2], and_23_out, in_5[2]);
  and and_31 (and_15_out[1], and_24_out, in_6[1]);
  and and_32 (and_15_out[2], and_24_out, in_6[2]);
  and and_33 (and_16_out[1], and_41_out, in_3[1]);
  and and_34 (and_16_out[2], and_41_out, in_3[2]);
  and and_35 (and_17_out[1], and_42_out, in_4[1]);
  and and_36 (and_17_out[2], and_42_out, in_4[2]);
  and and_37 (and_18_out[1], and_43_out, in_5[1]);
  and and_38 (and_18_out[2], and_43_out, in_5[2]);
  and and_39 (and_19_out[1], and_44_out, in_6[1]);
  and and_40 (and_19_out[2], and_44_out, in_6[2]);
  not not_12 (not_12_out, and_4_out);
  not not_13 (not_13_out, and_7_out);
  not not_14 (not_14_out, and_8_out);
  and and_41 (and_41_out, not_12_out, not_13_out, not_14_out, and_6_out);
  not not_15 (not_15_out, and_7_out);
  not not_16 (not_16_out, and_6_out);
  not not_17 (not_17_out, and_4_out);
  and and_42 (and_42_out, not_17_out, not_15_out, and_8_out, not_16_out);
  not not_18 (not_18_out, and_7_out);
  not not_19 (not_19_out, and_4_out);
  and and_43 (and_43_out, not_19_out, not_18_out, and_8_out, and_6_out);
  not not_20 (not_20_out, and_4_out);
  not not_21 (not_21_out, and_6_out);
  not not_22 (not_22_out, and_8_out);
  and and_44 (and_44_out, not_20_out, and_7_out, not_22_out, not_21_out);
  and and_45 (and_12_out[3], and_21_out, in_3[3]);
  and and_46 (and_12_out[4], and_21_out, in_3[4]);
  and and_47 (and_13_out[3], and_22_out, in_4[3]);
  and and_48 (and_13_out[4], and_22_out, in_4[4]);
  and and_49 (and_14_out[3], and_23_out, in_5[3]);
  and and_50 (and_14_out[4], and_23_out, in_5[4]);
  and and_51 (and_15_out[3], and_24_out, in_6[3]);
  and and_52 (and_15_out[4], and_24_out, in_6[4]);
  and and_53 (and_16_out[3], and_41_out, in_3[3]);
  and and_54 (and_16_out[4], and_41_out, in_3[4]);
  and and_55 (and_17_out[3], and_42_out, in_4[3]);
  and and_56 (and_17_out[4], and_42_out, in_4[4]);
  and and_57 (and_18_out[3], and_43_out, in_5[3]);
  and and_58 (and_18_out[4], and_43_out, in_5[4]);
  and and_59 (and_19_out[3], and_44_out, in_6[3]);
  and and_60 (and_19_out[4], and_44_out, in_6[4]);
  and and_61 (and_12_out[5], and_21_out, in_3[5]);
  and and_62 (and_13_out[5], and_22_out, in_4[5]);
  and and_63 (and_14_out[5], and_23_out, in_5[5]);
  and and_64 (and_15_out[5], and_24_out, in_6[5]);
  and and_65 (and_16_out[5], and_41_out, in_3[5]);
  and and_66 (and_17_out[5], and_42_out, in_4[5]);
  and and_67 (and_18_out[5], and_43_out, in_5[5]);
  and and_68 (and_19_out[5], and_44_out, in_6[5]);
  and and_69 (and_12_out[6], and_21_out, in_3[6]);
  and and_70 (and_13_out[6], and_22_out, in_4[6]);
  and and_71 (and_14_out[6], and_23_out, in_5[6]);
  and and_72 (and_15_out[6], and_24_out, in_6[6]);
  and and_73 (and_16_out[6], and_41_out, in_3[6]);
  and and_74 (and_17_out[6], and_42_out, in_4[6]);
  and and_75 (and_18_out[6], and_43_out, in_5[6]);
  and and_76 (and_19_out[6], and_44_out, in_6[6]);
  and and_77 (and_12_out[7], and_21_out, in_3[7]);
  and and_78 (and_13_out[7], and_22_out, in_4[7]);
  and and_79 (and_14_out[7], and_23_out, in_5[7]);
  and and_80 (and_15_out[7], and_24_out, in_6[7]);
  and and_81 (and_16_out[7], and_41_out, in_3[7]);
  and and_82 (and_17_out[7], and_42_out, in_4[7]);
  and and_83 (and_18_out[7], and_43_out, in_5[7]);
  and and_84 (and_19_out[7], and_44_out, in_6[7]);
  assign or_1_out = and_12_out | and_13_out | and_14_out | and_15_out;  // OR_Gate or_1, 8 bits wide
  assign or_2_out = and_16_out | and_17_out | and_18_out | and_19_out;  // OR_Gate or_2, 8 bits wide
  xor xor_1 (xor_1_out, or_1_out[0], or_2_out[0]);
  xor xor_2 (xor_2_out, or_1_out[1], or_2_out[1]);
  xor xor_3 (xor_3_out, or_1_out[2], or_2_out[2]);
  xor xor_4 (xor_4_out, or_1_out[3], or_2_out[3]);
  xor xor_5 (xor_5_out, or_1_out[4], or_2_out[4]);
  xor xor_6 (xor_6_out, or_1_out[5], or_2_out[5]);
  xor xor_7 (xor_7_out, or_1_out[6], or_2_out[6]);
  xor xor_8 (xor_8_out, or_1_out[7], or_2_out[7]);
  not not_23 (not_23_out, xor_1_out);
  not not_24 (not_24_out, xor_2_out);
  not not_25 (not_25_out, xor_3_out);
  not not_26 (not_26_out, xor_4_out);
  not not_27 (not_27_out, xor_5_out);
  not not_28 (not_28_out, xor_6_out);
  not not_29 (not_29_out, xor_7_out);
  not not_30 (not_30_out, xor_8_out);
  and and_85 (and_85_out, not_23_out, not_24_out, not_25_out, not_26_out, not_27_out, not_28_out, not_29_out, not_30_out);
  Register #(.width(1)) register_1 (.D(and_85_out), .Q(out_7), .clk(and_86_out));  // open: en, clr
  and and_86 (and_86_out, in_1, clock_1_out);
  Clock clock_1 (.out(clock_1_out));

  // Notes on the sheet:
  //   CMP
  //   First Register is A
  //   First Register is B
  //   First Register is C
  //   First Register is D
  //   Second Register is A
  //   Second Register is B
  //   Second Register is C
  //   Second Register is D
endmodule

module JE (
  input  [11:0] in_1,
  input  in_2,
  input  in_3,
  output [7:0] INSTRUCTION_ADDRESS_REGISTER
);

  wire and_1_out;

  and and_1 (and_1_out, in_2, in_3);
  and and_2 (INSTRUCTION_ADDRESS_REGISTER[7], and_1_out, in_1[11]);
  and and_3 (INSTRUCTION_ADDRESS_REGISTER[6], and_1_out, in_1[10]);
  and and_4 (INSTRUCTION_ADDRESS_REGISTER[5], and_1_out, in_1[9]);
  and and_5 (INSTRUCTION_ADDRESS_REGISTER[4], and_1_out, in_1[8]);
  and and_6 (INSTRUCTION_ADDRESS_REGISTER[3], and_1_out, in_1[7]);
  and and_7 (INSTRUCTION_ADDRESS_REGISTER[2], and_1_out, in_1[6]);
  and and_8 (INSTRUCTION_ADDRESS_REGISTER[1], and_1_out, in_1[5]);
  and and_9 (INSTRUCTION_ADDRESS_REGISTER[0], and_1_out, in_1[4]);
  // AND_Gate and_10 has open pins: in0=and_1_out, in1=in_1[3], out=open
  // AND_Gate and_11 has open pins: in0=and_1_out, in1=in_1[0], out=open
  // AND_Gate and_12 has open pins: in0=and_1_out, in1=in_1[1], out=open
  // AND_Gate and_13 has open pins: in0=and_1_out, in1=in_1[2], out=open

  // Notes on the sheet:
  //   JE
endmodule

module MEM (
  input  in_1,
  input  [11:0] in_2,
  input  [7:0] in_3,
  input  [7:0] in_4,
  input  [7:0] in_5,
  input  [7:0] in_6,
  output [7:0] MEMORY_ADDRESS,
  output [7:0] MEMORY_DATA,
  output UPDATE_MEMORY
);

  wire and_1_out, and_2_out, and_3_out, and_4_out, clock_1_out, not_1_out, not_2_out, not_3_out, not_4_out,
       not_5_out, not_6_out, not_7_out, not_8_out, not_9_out, not_10_out, not_11_out;
  wire [7:0] and_9_out, and_10_out, and_11_out, and_12_out;
  wire [7:7] and_18_out, and_19_out, and_20_out, and_21_out;

  and and_1 (and_1_out, in_1, in_2[11]);
  and and_2 (and_2_out, in_1, in_2[10]);
  and and_3 (and_3_out, in_1, in_2[9]);
  and and_4 (and_4_out, in_1, in_2[8]);
  and and_5 (MEMORY_ADDRESS[7], in_1, in_2[7]);
  and and_6 (MEMORY_ADDRESS[6], in_1, in_2[6]);
  and and_7 (MEMORY_ADDRESS[4], in_1, in_2[4]);
  and and_8 (MEMORY_ADDRESS[5], in_1, in_2[5]);
  assign and_9_out = {8{and_18_out[7]}} & in_3;  // AND_Gate and_9, 8 bits wide
  assign and_10_out = {8{and_19_out[7]}} & in_4;  // AND_Gate and_10, 8 bits wide
  assign and_11_out = {8{and_20_out[7]}} & in_5;  // AND_Gate and_11, 8 bits wide
  assign and_12_out = {8{and_21_out[7]}} & in_6;  // AND_Gate and_12, 8 bits wide
  Clock clock_1 (.out(clock_1_out));
  and and_13 (UPDATE_MEMORY, clock_1_out, in_1);
  and and_14 (MEMORY_ADDRESS[2], in_1, in_2[2]);
  and and_15 (MEMORY_ADDRESS[3], in_1, in_2[3]);
  and and_16 (MEMORY_ADDRESS[1], in_1, in_2[1]);
  and and_17 (MEMORY_ADDRESS[0], in_1, in_2[0]);
  not not_1 (not_1_out, and_2_out);
  not not_2 (not_2_out, and_1_out);
  not not_3 (not_3_out, and_3_out);
  and and_18 (and_18_out[7], not_2_out, not_1_out, not_3_out, and_4_out);
  not not_4 (not_4_out, and_1_out);
  not not_5 (not_5_out, and_2_out);
  not not_6 (not_6_out, and_4_out);
  and and_19 (and_19_out[7], not_4_out, not_5_out, and_3_out, not_6_out);
  not not_7 (not_7_out, and_1_out);
  not not_8 (not_8_out, and_2_out);
  and and_20 (and_20_out[7], not_7_out, not_8_out, and_3_out, and_4_out);
  not not_9 (not_9_out, and_3_out);
  not not_10 (not_10_out, and_4_out);
  not not_11 (not_11_out, and_1_out);
  and and_21 (and_21_out[7], not_11_out, and_2_out, not_9_out, not_10_out);
  assign MEMORY_DATA = and_9_out | and_10_out | and_11_out | and_12_out;  // OR_Gate or_1, 8 bits wide

  // Notes on the sheet:
  //   MEM
  //   First Register is A
  //   First Register is B
  //   First Register is C
  //   Second Register is D
endmodule

module LMEM (
  input  in_1,
  input  [11:0] in_2,
  input  [7:0] MEMORY_DATA,
  output [7:0] MEMORY_ADDRESS,
  output [7:0] REGISTER_A,
  output [7:0] REGISTER_B,
  output [7:0] REGISTER_C,
  output [7:0] REGISTER_D,
  output [3:0] UPDATE_REGISTER
);

  wire and_13_out, and_14_out, and_15_out, and_16_out, clock_1_out, not_1_out, not_2_out, not_3_out,
       not_4_out, not_5_out, not_6_out, not_7_out, not_8_out, not_9_out, not_10_out, not_11_out;
  wire [7:7] and_17_out, and_18_out, and_19_out, and_20_out;

  and and_1 (MEMORY_ADDRESS[6], in_1, in_2[10]);
  and and_2 (MEMORY_ADDRESS[5], in_1, in_2[9]);
  and and_3 (MEMORY_ADDRESS[7], in_1, in_2[11]);
  and and_4 (UPDATE_REGISTER[2], and_18_out[7], clock_1_out);
  and and_5 (UPDATE_REGISTER[3], and_17_out[7], clock_1_out);
  and and_6 (MEMORY_ADDRESS[3], in_1, in_2[7]);
  and and_7 (MEMORY_ADDRESS[4], in_1, in_2[8]);
  and and_8 (UPDATE_REGISTER[1], and_19_out[7], clock_1_out);
  and and_9 (UPDATE_REGISTER[0], and_20_out[7], clock_1_out);
  and and_10 (MEMORY_ADDRESS[1], in_1, in_2[5]);
  and and_11 (MEMORY_ADDRESS[2], in_1, in_2[6]);
  and and_12 (MEMORY_ADDRESS[0], in_1, in_2[4]);
  Clock clock_1 (.out(clock_1_out));
  and and_13 (and_13_out, in_1, in_2[1]);
  and and_14 (and_14_out, in_1, in_2[3]);
  and and_15 (and_15_out, in_1, in_2[2]);
  and and_16 (and_16_out, in_1, in_2[0]);
  not not_1 (not_1_out, and_15_out);
  not not_2 (not_2_out, and_13_out);
  not not_3 (not_3_out, and_14_out);
  and and_17 (and_17_out[7], not_3_out, not_1_out, not_2_out, and_16_out);
  not not_4 (not_4_out, and_15_out);
  not not_5 (not_5_out, and_16_out);
  not not_6 (not_6_out, and_14_out);
  and and_18 (and_18_out[7], not_6_out, not_4_out, and_13_out, not_5_out);
  not not_7 (not_7_out, and_14_out);
  not not_8 (not_8_out, and_15_out);
  and and_19 (and_19_out[7], not_7_out, not_8_out, and_13_out, and_16_out);
  not not_9 (not_9_out, and_16_out);
  not not_10 (not_10_out, and_13_out);
  not not_11 (not_11_out, and_14_out);
  and and_20 (and_20_out[7], not_11_out, and_15_out, not_10_out, not_9_out);
  assign REGISTER_A = {8{and_17_out[7]}} & MEMORY_DATA;  // AND_Gate and_21, 8 bits wide
  assign REGISTER_B = {8{and_18_out[7]}} & MEMORY_DATA;  // AND_Gate and_22, 8 bits wide
  assign REGISTER_C = {8{and_19_out[7]}} & MEMORY_DATA;  // AND_Gate and_23, 8 bits wide
  assign REGISTER_D = {8{and_20_out[7]}} & MEMORY_DATA;  // AND_Gate and_24, 8 bits wide

  // Notes on the sheet:
  //   LMEM
  //   First Register is A
  //   First Register is B
  //   First Register is C
  //   Second Register is D
endmodule

module INC (
  input  in_1,
  input  [11:0] in_2,
  input  [7:0] REGISTER_A,
  input  [7:0] REGISTER_B,
  input  [7:0] REGISTER_C,
  input  [7:0] REGISTER_D,
  output [7:0] REGISTER_A_2,
  output [7:0] REGISTER_B_2,
  output [7:0] REGISTER_C_2,
  output [7:0] REGISTER_D_2,
  output [3:0] UPDATE_REGISTER
);

  wire and_1_out, and_2_out, and_3_out, and_4_out, and_5_out, and_6_out, and_7_out, and_8_out, and_17_out,
       and_18_out, and_19_out, and_20_out, and_37_out, and_38_out, and_39_out, and_40_out, not_1_out,
       not_2_out, not_3_out, not_4_out, not_5_out, not_6_out, not_7_out, not_8_out, not_9_out, not_10_out,
       not_11_out, not_12_out, not_13_out, not_14_out, not_15_out, not_16_out, not_17_out, not_18_out,
       not_19_out, not_20_out, not_21_out, not_22_out, or_1_out;
  wire [3:0] and_16_out;
  wire [7:0] alu_1_out1, and_21_out, and_23_out, and_25_out, and_27_out, and_29_out, and_31_out, and_33_out,
       and_35_out, or_2_out, or_3_out;

  and and_1 (and_1_out, in_1, in_2[11]);
  and and_2 (and_2_out, in_1, in_2[10]);
  and and_3 (and_3_out, in_1, in_2[9]);
  and and_4 (and_4_out, in_1, in_2[7]);
  and and_5 (and_5_out, in_1, in_2[8]);
  and and_6 (and_6_out, in_1, in_2[5]);
  and and_7 (and_7_out, in_1, in_2[6]);
  and and_8 (and_8_out, in_1, in_2[4]);
  and and_9 (UPDATE_REGISTER[3], and_17_out, or_1_out);
  and and_10 (and_16_out[1], in_1, in_2[1]);
  and and_11 (and_16_out[2], in_1, in_2[2]);
  and and_12 (and_16_out[3], in_1, in_2[3]);
  or or_1 (or_1_out, alu_1_out1[0], alu_1_out1[1], alu_1_out1[2], alu_1_out1[3], alu_1_out1[4], alu_1_out1[5], alu_1_out1[6], alu_1_out1[7]);
  and and_13 (UPDATE_REGISTER[2], and_18_out, or_1_out);
  and and_14 (UPDATE_REGISTER[1], and_19_out, or_1_out);
  and and_15 (UPDATE_REGISTER[0], and_20_out, or_1_out);
  and and_16 (and_16_out[0], in_1, in_2[0]);
  not not_1 (not_1_out, and_2_out);
  not not_2 (not_2_out, and_3_out);
  not not_3 (not_3_out, and_1_out);
  and and_17 (and_17_out, not_3_out, not_1_out, not_2_out, and_5_out);
  not not_4 (not_4_out, and_5_out);
  not not_5 (not_5_out, and_1_out);
  not not_6 (not_6_out, and_2_out);
  and and_18 (and_18_out, not_5_out, not_6_out, and_3_out, not_4_out);
  not not_7 (not_7_out, and_1_out);
  not not_8 (not_8_out, and_2_out);
  and and_19 (and_19_out, not_7_out, not_8_out, and_3_out, and_5_out);
  not not_9 (not_9_out, and_3_out);
  not not_10 (not_10_out, and_5_out);
  not not_11 (not_11_out, and_1_out);
  and and_20 (and_20_out, not_11_out, and_2_out, not_9_out, not_10_out);
  and and_21 (and_21_out[0], and_17_out, REGISTER_A[0]);
  and and_22 (and_21_out[1], and_17_out, REGISTER_A[1]);
  and and_23 (and_23_out[0], and_18_out, REGISTER_B[0]);
  and and_24 (and_23_out[1], and_18_out, REGISTER_B[1]);
  and and_25 (and_25_out[0], and_19_out, REGISTER_C[0]);
  and and_26 (and_25_out[1], and_19_out, REGISTER_C[1]);
  and and_27 (and_27_out[0], and_20_out, REGISTER_D[0]);
  and and_28 (and_27_out[1], and_20_out, REGISTER_D[1]);
  and and_29 (and_29_out[0], and_37_out, REGISTER_A[0]);
  and and_30 (and_29_out[1], and_37_out, REGISTER_A[1]);
  and and_31 (and_31_out[0], and_38_out, REGISTER_B[0]);
  and and_32 (and_31_out[1], and_38_out, REGISTER_B[1]);
  and and_33 (and_33_out[0], and_39_out, REGISTER_C[0]);
  and and_34 (and_33_out[1], and_39_out, REGISTER_C[1]);
  and and_35 (and_35_out[0], and_40_out, REGISTER_D[0]);
  and and_36 (and_35_out[1], and_40_out, REGISTER_D[1]);
  not not_12 (not_12_out, and_6_out);
  not not_13 (not_13_out, and_4_out);
  not not_14 (not_14_out, and_7_out);
  and and_37 (and_37_out, not_13_out, not_14_out, not_12_out, and_8_out);
  not not_15 (not_15_out, and_8_out);
  not not_16 (not_16_out, and_7_out);
  not not_17 (not_17_out, and_4_out);
  and and_38 (and_38_out, not_17_out, not_16_out, and_6_out, not_15_out);
  not not_18 (not_18_out, and_7_out);
  not not_19 (not_19_out, and_4_out);
  and and_39 (and_39_out, not_19_out, not_18_out, and_6_out, and_8_out);
  not not_20 (not_20_out, and_6_out);
  not not_21 (not_21_out, and_8_out);
  not not_22 (not_22_out, and_4_out);
  and and_40 (and_40_out, not_22_out, and_7_out, not_20_out, not_21_out);
  and and_41 (and_21_out[2], and_17_out, REGISTER_A[2]);
  and and_42 (and_21_out[3], and_17_out, REGISTER_A[3]);
  and and_43 (and_23_out[2], and_18_out, REGISTER_B[2]);
  and and_44 (and_23_out[3], and_18_out, REGISTER_B[3]);
  and and_45 (and_25_out[2], and_19_out, REGISTER_C[2]);
  and and_46 (and_25_out[3], and_19_out, REGISTER_C[3]);
  and and_47 (and_27_out[2], and_20_out, REGISTER_D[2]);
  and and_48 (and_27_out[3], and_20_out, REGISTER_D[3]);
  and and_49 (and_29_out[2], and_37_out, REGISTER_A[2]);
  and and_50 (and_29_out[3], and_37_out, REGISTER_A[3]);
  and and_51 (and_31_out[2], and_38_out, REGISTER_B[2]);
  and and_52 (and_31_out[3], and_38_out, REGISTER_B[3]);
  and and_53 (and_33_out[2], and_39_out, REGISTER_C[2]);
  and and_54 (and_33_out[3], and_39_out, REGISTER_C[3]);
  and and_55 (and_35_out[2], and_40_out, REGISTER_D[2]);
  and and_56 (and_35_out[3], and_40_out, REGISTER_D[3]);
  and and_57 (and_21_out[4], and_17_out, REGISTER_A[4]);
  and and_58 (and_23_out[4], and_18_out, REGISTER_B[4]);
  and and_59 (and_25_out[4], and_19_out, REGISTER_C[4]);
  and and_60 (and_27_out[4], and_20_out, REGISTER_D[4]);
  and and_61 (and_29_out[4], and_37_out, REGISTER_A[4]);
  and and_62 (and_31_out[4], and_38_out, REGISTER_B[4]);
  and and_63 (and_31_out[5], and_38_out, REGISTER_B[5]);
  and and_64 (and_33_out[4], and_39_out, REGISTER_C[4]);
  and and_65 (and_33_out[5], and_39_out, REGISTER_C[5]);
  and and_66 (and_35_out[4], and_40_out, REGISTER_D[4]);
  and and_67 (and_35_out[5], and_40_out, REGISTER_D[5]);
  and and_68 (and_21_out[5], and_17_out, REGISTER_A[5]);
  and and_69 (and_21_out[6], and_17_out, REGISTER_A[6]);
  and and_70 (and_23_out[5], and_18_out, REGISTER_B[5]);
  and and_71 (and_23_out[6], and_18_out, REGISTER_B[6]);
  and and_72 (and_25_out[5], and_19_out, REGISTER_C[5]);
  and and_73 (and_25_out[6], and_19_out, REGISTER_C[6]);
  and and_74 (and_27_out[5], and_20_out, REGISTER_D[5]);
  and and_75 (and_27_out[6], and_20_out, REGISTER_D[6]);
  and and_76 (and_29_out[5], and_37_out, REGISTER_A[5]);
  and and_77 (and_29_out[6], and_37_out, REGISTER_A[6]);
  and and_78 (and_31_out[6], and_38_out, REGISTER_B[6]);
  and and_79 (and_33_out[6], and_39_out, REGISTER_C[6]);
  and and_80 (and_35_out[6], and_40_out, REGISTER_D[6]);
  and and_81 (and_21_out[7], and_17_out, REGISTER_A[7]);
  and and_82 (and_23_out[7], and_18_out, REGISTER_B[7]);
  and and_83 (and_25_out[7], and_19_out, REGISTER_C[7]);
  and and_84 (and_27_out[7], and_20_out, REGISTER_D[7]);
  and and_85 (and_29_out[7], and_37_out, REGISTER_A[7]);
  and and_86 (and_31_out[7], and_38_out, REGISTER_B[7]);
  and and_87 (and_33_out[7], and_39_out, REGISTER_C[7]);
  and and_88 (and_35_out[7], and_40_out, REGISTER_D[7]);
  assign or_2_out = and_21_out | and_23_out | and_25_out | and_27_out;  // OR_Gate or_2, 8 bits wide
  assign or_3_out = and_29_out | and_31_out | and_33_out | and_35_out;  // OR_Gate or_3, 8 bits wide
  ALU alu_1 (
    .OUT1(alu_1_out1[0]), .OUT2(alu_1_out1[1]), .OUT3(alu_1_out1[2]), .OUT4(alu_1_out1[3]),
    .OUT5(alu_1_out1[4]), .OUT6(alu_1_out1[5]), .OUT7(alu_1_out1[6]), .OUT8(alu_1_out1[7]), .in_1(1'b0),
    .in_2(or_3_out[7]), .in_3(or_3_out[6]), .in_4(or_3_out[5]), .INPUT_2(or_3_out[4]), .in_6(or_3_out[3]),
    .in_7(or_3_out[2]), .in_8(or_3_out[1]), .in_9(or_3_out[0]), .in_10(or_2_out[7]), .in_11(or_2_out[6]),
    .in_12(or_2_out[5]), .in_13(or_2_out[4]), .in_14(or_2_out[3]), .in_15(or_2_out[2]), .in_16(or_2_out[1]),
    .in_17(or_2_out[0]));  // open: Overflow, NEGATIVE, Zero
  and and_89 (REGISTER_A_2[0], and_17_out, alu_1_out1[0]);
  and and_90 (REGISTER_A_2[1], and_17_out, alu_1_out1[1]);
  and and_91 (REGISTER_B_2[0], and_18_out, alu_1_out1[0]);
  and and_92 (REGISTER_B_2[1], and_18_out, alu_1_out1[1]);
  and and_93 (REGISTER_C_2[0], and_19_out, alu_1_out1[0]);
  and and_94 (REGISTER_C_2[1], and_19_out, alu_1_out1[1]);
  and and_95 (REGISTER_D_2[0], and_20_out, alu_1_out1[0]);
  and and_96 (REGISTER_D_2[1], and_20_out, alu_1_out1[1]);
  and and_97 (REGISTER_A_2[2], and_17_out, alu_1_out1[2]);
  and and_98 (REGISTER_A_2[3], and_17_out, alu_1_out1[3]);
  and and_99 (REGISTER_B_2[2], and_18_out, alu_1_out1[2]);
  and and_100 (REGISTER_B_2[3], and_18_out, alu_1_out1[3]);
  and and_101 (REGISTER_C_2[2], and_19_out, alu_1_out1[2]);
  and and_102 (REGISTER_C_2[3], and_19_out, alu_1_out1[3]);
  and and_103 (REGISTER_D_2[2], and_20_out, alu_1_out1[2]);
  and and_104 (REGISTER_D_2[3], and_20_out, alu_1_out1[3]);
  and and_105 (REGISTER_A_2[4], and_17_out, alu_1_out1[4]);
  and and_106 (REGISTER_A_2[5], and_17_out, alu_1_out1[5]);
  and and_107 (REGISTER_B_2[4], and_18_out, alu_1_out1[4]);
  and and_108 (REGISTER_B_2[5], and_18_out, alu_1_out1[5]);
  and and_109 (REGISTER_C_2[4], and_19_out, alu_1_out1[4]);
  and and_110 (REGISTER_C_2[5], and_19_out, alu_1_out1[5]);
  and and_111 (REGISTER_D_2[4], and_20_out, alu_1_out1[4]);
  and and_112 (REGISTER_D_2[5], and_20_out, alu_1_out1[5]);
  and and_113 (REGISTER_A_2[6], and_17_out, alu_1_out1[6]);
  and and_114 (REGISTER_B_2[6], and_18_out, alu_1_out1[6]);
  and and_115 (REGISTER_C_2[6], and_19_out, alu_1_out1[6]);
  and and_116 (REGISTER_D_2[6], and_20_out, alu_1_out1[6]);
  and and_117 (REGISTER_A_2[7], and_17_out, alu_1_out1[7]);
  and and_118 (REGISTER_B_2[7], and_18_out, alu_1_out1[7]);
  and and_119 (REGISTER_C_2[7], and_19_out, alu_1_out1[7]);
  and and_120 (REGISTER_D_2[7], and_20_out, alu_1_out1[7]);

  // Notes on the sheet:
  //   INC
  //   First Register is A
  //   First Register is B
  //   First Register is C
  //   First Register is D
  //   Second Register is A
  //   Second Register is B
  //   Second Register is C
  //   Second Register is D
endmodule

module DEC (
  input  in_1,
  input  [11:0] in_2,
  input  [7:0] REGISTER_A,
  input  [7:0] REGISTER_B,
  input  [7:0] REGISTER_C,
  input  [7:0] REGISTER_D,
  output [7:0] REGISTER_A_2,
  output [7:0] REGISTER_B_2,
  output [7:0] REGISTER_C_2,
  output [7:0] REGISTER_D_2,
  output [3:0] UPDATE_REGISTER
);

  wire and_1_out, and_2_out, and_3_out, and_4_out, and_5_out, and_6_out, and_7_out, and_8_out, and_17_out,
       and_18_out, and_19_out, and_20_out, and_37_out, and_38_out, and_39_out, and_40_out, not_1_out,
       not_2_out, not_3_out, not_4_out, not_5_out, not_6_out, not_7_out, not_8_out, not_9_out, not_10_out,
       not_11_out, not_12_out, not_13_out, not_14_out, not_15_out, not_16_out, not_17_out, not_18_out,
       not_19_out, not_20_out, not_21_out, not_22_out, or_1_out;
  wire [3:0] and_16_out;
  wire [7:0] alu_1_out1, and_21_out, and_23_out, and_25_out, and_27_out, and_29_out, and_31_out, and_33_out,
       and_35_out, or_2_out, or_3_out;

  and and_1 (and_1_out, in_1, in_2[11]);
  and and_2 (and_2_out, in_1, in_2[9]);
  and and_3 (and_3_out, in_1, in_2[10]);
  and and_4 (and_4_out, in_1, in_2[7]);
  and and_5 (and_5_out, in_1, in_2[8]);
  and and_6 (and_6_out, in_1, in_2[6]);
  and and_7 (and_7_out, in_1, in_2[4]);
  and and_8 (and_8_out, in_1, in_2[5]);
  and and_9 (UPDATE_REGISTER[3], and_17_out, or_1_out);
  and and_10 (and_16_out[2], in_1, in_2[2]);
  and and_11 (and_16_out[1], in_1, in_2[1]);
  and and_12 (and_16_out[3], in_1, in_2[3]);
  or or_1 (or_1_out, alu_1_out1[0], alu_1_out1[1], alu_1_out1[2], alu_1_out1[3], alu_1_out1[4], alu_1_out1[5], alu_1_out1[6], alu_1_out1[7]);
  and and_13 (UPDATE_REGISTER[0], and_20_out, or_1_out);
  and and_14 (UPDATE_REGISTER[2], and_18_out, or_1_out);
  and and_15 (UPDATE_REGISTER[1], and_19_out, or_1_out);
  and and_16 (and_16_out[0], in_1, in_2[0]);
  not not_1 (not_1_out, and_1_out);
  not not_2 (not_2_out, and_3_out);
  not not_3 (not_3_out, and_2_out);
  and and_17 (and_17_out, not_1_out, not_2_out, not_3_out, and_5_out);
  not not_4 (not_4_out, and_3_out);
  not not_5 (not_5_out, and_5_out);
  not not_6 (not_6_out, and_1_out);
  and and_18 (and_18_out, not_6_out, not_4_out, and_2_out, not_5_out);
  not not_7 (not_7_out, and_3_out);
  not not_8 (not_8_out, and_1_out);
  and and_19 (and_19_out, not_8_out, not_7_out, and_2_out, and_5_out);
  not not_9 (not_9_out, and_1_out);
  not not_10 (not_10_out, and_5_out);
  not not_11 (not_11_out, and_2_out);
  and and_20 (and_20_out, not_9_out, and_3_out, not_11_out, not_10_out);
  and and_21 (and_21_out[0], and_17_out, REGISTER_A[0]);
  and and_22 (and_21_out[1], and_17_out, REGISTER_A[1]);
  and and_23 (and_23_out[0], and_18_out, REGISTER_B[0]);
  and and_24 (and_23_out[1], and_18_out, REGISTER_B[1]);
  and and_25 (and_25_out[0], and_19_out, REGISTER_C[0]);
  and and_26 (and_25_out[1], and_19_out, REGISTER_C[1]);
  and and_27 (and_27_out[0], and_20_out, REGISTER_D[0]);
  and and_28 (and_27_out[1], and_20_out, REGISTER_D[1]);
  and and_29 (and_29_out[0], and_37_out, REGISTER_A[0]);
  and and_30 (and_29_out[1], and_37_out, REGISTER_A[1]);
  and and_31 (and_31_out[0], and_38_out, REGISTER_B[0]);
  and and_32 (and_31_out[1], and_38_out, REGISTER_B[1]);
  and and_33 (and_33_out[0], and_39_out, REGISTER_C[0]);
  and and_34 (and_33_out[1], and_39_out, REGISTER_C[1]);
  and and_35 (and_35_out[0], and_40_out, REGISTER_D[0]);
  and and_36 (and_35_out[1], and_40_out, REGISTER_D[1]);
  not not_12 (not_12_out, and_8_out);
  not not_13 (not_13_out, and_6_out);
  not not_14 (not_14_out, and_4_out);
  and and_37 (and_37_out, not_14_out, not_13_out, not_12_out, and_7_out);
  not not_15 (not_15_out, and_4_out);
  not not_16 (not_16_out, and_7_out);
  not not_17 (not_17_out, and_6_out);
  and and_38 (and_38_out, not_15_out, not_17_out, and_8_out, not_16_out);
  not not_18 (not_18_out, and_4_out);
  not not_19 (not_19_out, and_6_out);
  and and_39 (and_39_out, not_18_out, not_19_out, and_8_out, and_7_out);
  not not_20 (not_20_out, and_8_out);
  not not_21 (not_21_out, and_7_out);
  not not_22 (not_22_out, and_4_out);
  and and_40 (and_40_out, not_22_out, and_6_out, not_20_out, not_21_out);
  and and_41 (and_21_out[2], and_17_out, REGISTER_A[2]);
  and and_42 (and_21_out[3], and_17_out, REGISTER_A[3]);
  and and_43 (and_23_out[2], and_18_out, REGISTER_B[2]);
  and and_44 (and_23_out[3], and_18_out, REGISTER_B[3]);
  and and_45 (and_25_out[2], and_19_out, REGISTER_C[2]);
  and and_46 (and_25_out[3], and_19_out, REGISTER_C[3]);
  and and_47 (and_27_out[2], and_20_out, REGISTER_D[2]);
  and and_48 (and_27_out[3], and_20_out, REGISTER_D[3]);
  and and_49 (and_29_out[2], and_37_out, REGISTER_A[2]);
  and and_50 (and_29_out[3], and_37_out, REGISTER_A[3]);
  and and_51 (and_31_out[2], and_38_out, REGISTER_B[2]);
  and and_52 (and_31_out[3], and_38_out, REGISTER_B[3]);
  and and_53 (and_33_out[2], and_39_out, REGISTER_C[2]);
  and and_54 (and_33_out[3], and_39_out, REGISTER_C[3]);
  and and_55 (and_35_out[2], and_40_out, REGISTER_D[2]);
  and and_56 (and_35_out[3], and_40_out, REGISTER_D[3]);
  and and_57 (and_21_out[4], and_17_out, REGISTER_A[4]);
  and and_58 (and_23_out[4], and_18_out, REGISTER_B[4]);
  and and_59 (and_25_out[4], and_19_out, REGISTER_C[4]);
  and and_60 (and_27_out[4], and_20_out, REGISTER_D[4]);
  and and_61 (and_29_out[4], and_37_out, REGISTER_A[4]);
  and and_62 (and_31_out[4], and_38_out, REGISTER_B[4]);
  and and_63 (and_31_out[5], and_38_out, REGISTER_B[5]);
  and and_64 (and_33_out[4], and_39_out, REGISTER_C[4]);
  and and_65 (and_33_out[5], and_39_out, REGISTER_C[5]);
  and and_66 (and_35_out[4], and_40_out, REGISTER_D[4]);
  and and_67 (and_35_out[5], and_40_out, REGISTER_D[5]);
  and and_68 (and_21_out[5], and_17_out, REGISTER_A[5]);
  and and_69 (and_21_out[6], and_17_out, REGISTER_A[6]);
  and and_70 (and_23_out[5], and_18_out, REGISTER_B[5]);
  and and_71 (and_23_out[6], and_18_out, REGISTER_B[6]);
  and and_72 (and_25_out[5], and_19_out, REGISTER_C[5]);
  and and_73 (and_25_out[6], and_19_out, REGISTER_C[6]);
  and and_74 (and_27_out[5], and_20_out, REGISTER_D[5]);
  and and_75 (and_27_out[6], and_20_out, REGISTER_D[6]);
  and and_76 (and_29_out[5], and_37_out, REGISTER_A[5]);
  and and_77 (and_29_out[6], and_37_out, REGISTER_A[6]);
  and and_78 (and_31_out[6], and_38_out, REGISTER_B[6]);
  and and_79 (and_33_out[6], and_39_out, REGISTER_C[6]);
  and and_80 (and_35_out[6], and_40_out, REGISTER_D[6]);
  and and_81 (and_21_out[7], and_17_out, REGISTER_A[7]);
  and and_82 (and_23_out[7], and_18_out, REGISTER_B[7]);
  and and_83 (and_25_out[7], and_19_out, REGISTER_C[7]);
  and and_84 (and_27_out[7], and_20_out, REGISTER_D[7]);
  and and_85 (and_29_out[7], and_37_out, REGISTER_A[7]);
  and and_86 (and_31_out[7], and_38_out, REGISTER_B[7]);
  and and_87 (and_33_out[7], and_39_out, REGISTER_C[7]);
  and and_88 (and_35_out[7], and_40_out, REGISTER_D[7]);
  assign or_2_out = and_21_out | and_23_out | and_25_out | and_27_out;  // OR_Gate or_2, 8 bits wide
  assign or_3_out = and_29_out | and_31_out | and_33_out | and_35_out;  // OR_Gate or_3, 8 bits wide
  ALU alu_1 (
    .OUT1(alu_1_out1[0]), .OUT2(alu_1_out1[1]), .OUT3(alu_1_out1[2]), .OUT4(alu_1_out1[3]),
    .OUT5(alu_1_out1[4]), .OUT6(alu_1_out1[5]), .OUT7(alu_1_out1[6]), .OUT8(alu_1_out1[7]), .in_1(1'b1),
    .in_2(or_3_out[7]), .in_3(or_3_out[6]), .in_4(or_3_out[5]), .INPUT_2(or_3_out[4]), .in_6(or_3_out[3]),
    .in_7(or_3_out[2]), .in_8(or_3_out[1]), .in_9(or_3_out[0]), .in_10(or_2_out[7]), .in_11(or_2_out[6]),
    .in_12(or_2_out[5]), .in_13(or_2_out[4]), .in_14(or_2_out[3]), .in_15(or_2_out[2]), .in_16(or_2_out[1]),
    .in_17(or_2_out[0]));  // open: Overflow, NEGATIVE, Zero
  and and_89 (REGISTER_A_2[0], and_17_out, alu_1_out1[0]);
  and and_90 (REGISTER_A_2[1], and_17_out, alu_1_out1[1]);
  and and_91 (REGISTER_B_2[0], and_18_out, alu_1_out1[0]);
  and and_92 (REGISTER_B_2[1], and_18_out, alu_1_out1[1]);
  and and_93 (REGISTER_C_2[0], and_19_out, alu_1_out1[0]);
  and and_94 (REGISTER_C_2[1], and_19_out, alu_1_out1[1]);
  and and_95 (REGISTER_D_2[0], and_20_out, alu_1_out1[0]);
  and and_96 (REGISTER_D_2[1], and_20_out, alu_1_out1[1]);
  and and_97 (REGISTER_A_2[2], and_17_out, alu_1_out1[2]);
  and and_98 (REGISTER_A_2[3], and_17_out, alu_1_out1[3]);
  and and_99 (REGISTER_B_2[2], and_18_out, alu_1_out1[2]);
  and and_100 (REGISTER_B_2[3], and_18_out, alu_1_out1[3]);
  and and_101 (REGISTER_C_2[2], and_19_out, alu_1_out1[2]);
  and and_102 (REGISTER_C_2[3], and_19_out, alu_1_out1[3]);
  and and_103 (REGISTER_D_2[2], and_20_out, alu_1_out1[2]);
  and and_104 (REGISTER_D_2[3], and_20_out, alu_1_out1[3]);
  and and_105 (REGISTER_A_2[4], and_17_out, alu_1_out1[4]);
  and and_106 (REGISTER_A_2[5], and_17_out, alu_1_out1[5]);
  and and_107 (REGISTER_B_2[4], and_18_out, alu_1_out1[4]);
  and and_108 (REGISTER_B_2[5], and_18_out, alu_1_out1[5]);
  and and_109 (REGISTER_C_2[4], and_19_out, alu_1_out1[4]);
  and and_110 (REGISTER_C_2[5], and_19_out, alu_1_out1[5]);
  and and_111 (REGISTER_D_2[4], and_20_out, alu_1_out1[4]);
  and and_112 (REGISTER_D_2[5], and_20_out, alu_1_out1[5]);
  and and_113 (REGISTER_A_2[6], and_17_out, alu_1_out1[6]);
  and and_114 (REGISTER_B_2[6], and_18_out, alu_1_out1[6]);
  and and_115 (REGISTER_C_2[6], and_19_out, alu_1_out1[6]);
  and and_116 (REGISTER_D_2[6], and_20_out, alu_1_out1[6]);
  and and_117 (REGISTER_A_2[7], and_17_out, alu_1_out1[7]);
  and and_118 (REGISTER_B_2[7], and_18_out, alu_1_out1[7]);
  and and_119 (REGISTER_C_2[7], and_19_out, alu_1_out1[7]);
  and and_120 (REGISTER_D_2[7], and_20_out, alu_1_out1[7]);

  // Notes on the sheet:
  //   DEC
  //   First Register is A
  //   First Register is B
  //   First Register is C
  //   First Register is D
  //   Second Register is A
  //   Second Register is B
  //   Second Register is C
  //   Second Register is D
endmodule
