// Logisim project CPU - Mainboard.circ as structural Verilog: 17 circuits, main circuit CPU
module Mainboard (
);

  wire button_1_out, clock_1_out, cpu_1_ram_clk, cpu_1_ram_we, d_ff_1_q, keyboard_1_avail, or_1_out,
       or_2_out, or_3_out, switch_1_p2;
  wire [3:0] cpu_1_second_out, cpu_1_second_out_2, register_1_q;
  wire [6:0] buzzer_1_p3, demultiplexer_1_out2, keyboard_1_data;
  wire [7:0] cpu_1_main_out, cpu_1_ram_addr, cpu_1_ram_out, or_4_out, ram_1_dout;
  wire [7:7] demultiplexer_1_out0, demultiplexer_1_out1, demultiplexer_1_out2_2, demultiplexer_1_out3;
  wire [11:0] cpu_1_rom_addr;
  wire [15:0] rom_1_data;

  Keyboard #(.buflen(1)) keyboard_1 (
    .clr(keyboard_1_avail), .avail(keyboard_1_avail), .data(keyboard_1_data));  // open: clk, re
  or or_1 (or_1_out, cpu_1_second_out[0], cpu_1_second_out[1], cpu_1_second_out[2], cpu_1_second_out[3], cpu_1_second_out_2[0], cpu_1_second_out_2[1], cpu_1_second_out_2[2], cpu_1_second_out_2[3]);
  Clock clock_1 (.out(clock_1_out));
  TTY #(.cols(26)) tty_1 (.data(demultiplexer_1_out2), .clk(clock_1_out), .clr(button_1_out));  // open: we
  // Switch switch_1: pin names not known; wires that end beside it: 1'b1, switch_1_p2
  Button button_1 (.out(button_1_out));
  Register #(.width(4)) register_1 (
    .D(cpu_1_second_out), .en(or_1_out), .clk(or_1_out), .Q(register_1_q), .clr(button_1_out));
  Demultiplexer #(.select(4), .width(8)) demultiplexer_1 (
    .out0({8{demultiplexer_1_out0[7]}}), .out1({8{demultiplexer_1_out1[7]}}),
    .out2({demultiplexer_1_out2_2[7], demultiplexer_1_out2}), .out3({8{demultiplexer_1_out3[7]}}),
    .in(cpu_1_main_out), .sel(register_1_q));  // open: out4, out5, out6, out7, out8, out9, out10, out11, out12, out13, out14, out15
  CPU cpu_1 (
    .ENABLE(switch_1_p2), .RESET(button_1_out), .RAM_IN(ram_1_dout), .ROM_DATA(rom_1_data),
    .MAIN_OUT(cpu_1_main_out), .SECOND_OUT({cpu_1_second_out_2, cpu_1_second_out}),
    .ROM_ADDR(cpu_1_rom_addr), .RAM_ADDR(cpu_1_ram_addr), .RAM_WE(cpu_1_ram_we), .RAM_CLK(cpu_1_ram_clk),
    .RAM_OUT(cpu_1_ram_out));  // open: MAIN_INPUT
  Hex_Digit_Display hex_digit_display_1 (.value(cpu_1_second_out_2));  // open: dp
  Hex_Digit_Display hex_digit_display_2 (.value(cpu_1_main_out[7:4]));  // open: dp
  Hex_Digit_Display hex_digit_display_3 (.value(cpu_1_second_out));  // open: dp
  or or_2 (or_2_out, keyboard_1_avail, cpu_1_ram_we);
  or or_3 (or_3_out, cpu_1_ram_clk, keyboard_1_avail);
  Hex_Digit_Display hex_digit_display_4 (.value(cpu_1_main_out[3:0]));  // open: dp
  ROM #(.addrWidth(12), .dataWidth(16)) rom_1 (.addr(cpu_1_rom_addr), .data(rom_1_data));
  RAM #(.clearpin("true"), .enables("line")) ram_1 (
    .addr(cpu_1_ram_addr), .we(or_2_out), .clk(or_3_out), .din(or_4_out), .dout(ram_1_dout),
    .clr(button_1_out));
  assign or_4_out = cpu_1_ram_out | {1'b0, keyboard_1_data};  // OR_Gate or_4, 8 bits wide
  D_Flip_Flop d_ff_1 (
    .D(demultiplexer_1_out0[7]), .clk(demultiplexer_1_out0[7]), .Q(d_ff_1_q), .reset(demultiplexer_1_out1[7]));  // open: Qn, preset
  // Buzzer #(.waveform("Triangle")) buzzer_1: pin names not known; wires that end beside it: 14'ha0f, d_ff_1_q, buzzer_1_p3
  Slider #(.width(7)) slider_1 (.out(buzzer_1_p3));

  // Notes on the sheet:
  //   contents of rom_1 (hex, n*v repeats v):
  //   92ff 9301 2301 a200 730a 8008 5002 0 9201 0 a200 92ff a200 9202 0 a200 e200 a200 9300 c300 5010
endmodule

module CPU (
  input  [15:0] ROM_DATA,
  input  ENABLE,
  input  RESET,
  input  [7:0] RAM_IN,
  input  [7:0] MAIN_INPUT,
  output [11:0] ROM_ADDR,
  output [7:0] RAM_ADDR,
  output RAM_WE,
  output RAM_CLK,
  output [7:0] RAM_OUT,
  output [7:0] MAIN_OUT,
  output [7:0] SECOND_OUT
);

  wire and_3_out, CLK, clock_2_out, cmp2_1_equals, CMP2I, cmp_1_equals, CMPI, CMPOT, DEC2_ERROR, DEC2I,
       DEC_ERROR, DECI, decoder_1_out0, decoder_2_out1, decoder_2_out2, decoder_2_out3, decoder_2_out4,
       decoder_2_out5, decoder_2_out6, INBI, INC2_ERROR, INC2I, INC_ERROR, INCI, INV_CLK, JE_PER, JEI, JMPI,
       LMEM2I, LMEMI, MEM2_UPDATE, MEM2I, MEM_UPDATE, MEMI, or_1_out, or_14_out, or_15_out, or_16_out,
       or_17_out, or_18_out, or_19_out, or_20_out, or_21_out, or_22_out, OUTBI, OUTSEL, SETI;
  wire [3:0] and_1_out, DEC2_UPDATE_REG, DEC_UPDATE_REG, INB_UPDATE_REG, INC2_UPDATE_REG, INC_UPDATE_REG,
       LMEM2_UPDATE, LMEM_UPDATE, or_7_out, SET_UPDATE_REG;
  wire [7:0] AOUT, BOUT, COUT, DEC2_EQUALS, DEC_EQUALS, DOUT, EOUT, FOUT, INB_OUT, INC2_EQUALS, INC_EQUALS,
       LMEM2_ADDRESS, LMEM2_OUTPUT, LMEM_ADDRESS, LMEM_OUTPUT, MEM2_ADDRESS, MEM2_OUTPUT, MEM_ADDRESS,
       MEM_OUTPUT, not_3_out, or_8_out, or_9_out, or_10_out, or_11_out, or_12_out, or_13_out, outb_1_cpu_out,
       SET_OUT;
  wire [11:0] adder_1_out, and_2_out, IDATA, or_2_out, PM_JE_OUT, PM_JUMP_OUT;
  wire [11:11] not_2_out;

  Clock clock_1 (.out(CLK));
  Decoder #(.select(4)) decoder_1 (
    .out0(decoder_1_out0), .out1(INCI), .out2(INC2I), .out3(DECI), .out4(DEC2I), .out5(JMPI), .out6(CMPI),
    .out7(CMP2I), .out8(JEI), .out9(SETI), .out10(OUTBI), .out11(INBI), .out12(MEMI), .out13(MEM2I),
    .out14(LMEMI), .out15(LMEM2I), .sel(and_1_out));  // open: en
  not not_1 (INV_CLK, CLK);
  or or_1 (or_1_out, JMPI, JE_PER);
  INC inc_1 (
    .ENABLE(INCI), .IDATA(IDATA), .REGISTER_A(AOUT), .REGISTER_B(BOUT), .REGISTER_C(COUT), .REGISTER_D(DOUT),
    .REGISTER_E(EOUT), .REGISTER_F(FOUT), .EQUALS(INC_EQUALS), .ERROR(INC_ERROR), .UPDATE_REG(INC_UPDATE_REG));
  JMP jmp_1 (.ENABLE(JMPI), .IDATA(IDATA), .PM(PM_JUMP_OUT));
  MEM mem_1 (
    .ENABLE(MEMI), .IDATA(IDATA), .REGISTER_A(AOUT), .REGISTER_B(BOUT), .REGISTER_C(COUT), .REGISTER_D(DOUT),
    .REGISTER_E(EOUT), .REGISTER_F(FOUT), .RAM_ADDRESS(MEM_ADDRESS), .EQUALS(MEM_OUTPUT),
    .UPDATE_RAM(MEM_UPDATE));
  MEM2 mem2_1 (
    .ENABLE(MEM2I), .IDATA(IDATA), .REGISTER_A(AOUT), .REGISTER_B(BOUT), .REGISTER_C(COUT),
    .REGISTER_D(DOUT), .REGISTER_E(EOUT), .REGISTER_F(FOUT), .MEM_OUT(MEM2_ADDRESS),
    .MEM_ADDRESS(MEM2_OUTPUT), .UPDATE_RAM(MEM2_UPDATE));
  LMEM lmem_1 (
    .ENABLE(LMEMI), .IDATA(IDATA), .RAM(RAM_IN), .RAM_ADDRESS(LMEM_ADDRESS), .RAM_OUT(LMEM_OUTPUT),
    .UPDATE_REG(LMEM_UPDATE));
  LMEM2 lmem2_1 (
    .ENABLE(LMEM2I), .IDATA(IDATA), .A(AOUT), .B(BOUT), .C(COUT), .D(DOUT), .E(EOUT), .F(FOUT), .RAM(RAM_IN),
    .RAM_ADDRESS(LMEM2_ADDRESS), .RAM_OUT(LMEM2_OUTPUT), .UPDATE_REG(LMEM2_UPDATE));
  not not_2 (not_2_out[11], or_1_out);
  assign {and_1_out, IDATA} = ROM_DATA & {16{ENABLE}};  // AND_Gate and_1, 16 bits wide
  assign and_2_out = {12{not_2_out[11]}} & adder_1_out;  // AND_Gate and_2, 12 bits wide
  Register #(.width(12)) ProgramCounter (.D(or_2_out), .clk(and_3_out), .Q(ROM_ADDR), .clr(RESET));  // open: en
  assign or_2_out = and_2_out | PM_JE_OUT | PM_JUMP_OUT;  // OR_Gate or_2, 12 bits wide
  and and_3 (and_3_out, ENABLE, CLK);
  Adder #(.width(12)) adder_1 (.a(ROM_ADDR), .b(12'h1), .out(adder_1_out));  // open: cin, cout
  or or_3 (RAM_WE, MEM2I, MEMI);
  or or_4 (RAM_CLK, MEM2_UPDATE, MEM_UPDATE);
  INC2 inc2_1 (
    .ENABLE(INC2I), .IDATA(IDATA), .REGISTER_A(AOUT), .REGISTER_B(BOUT), .REGISTER_C(COUT),
    .REGISTER_D(DOUT), .REGISTER_E(EOUT), .REGISTER_F(FOUT), .EQUALS(INC2_EQUALS), .ERROR(INC2_ERROR),
    .UPDATE_REG(INC2_UPDATE_REG));
  CMP cmp_1 (
    .ENABLE(CMPI), .IDATA(IDATA), .REGISTER_A(AOUT), .REGISTER_B(BOUT), .REGISTER_C(COUT), .REGISTER_D(DOUT),
    .REGISTER_E(EOUT), .REGISTER_F(FOUT), .EQUALS(cmp_1_equals));
  CMP2 cmp2_1 (
    .ENABLE(CMP2I), .IDATA(IDATA), .REGISTER_A(AOUT), .REGISTER_B(BOUT), .REGISTER_C(COUT),
    .REGISTER_D(DOUT), .REGISTER_E(EOUT), .REGISTER_F(FOUT), .EQUALS(cmp2_1_equals));
  Register #(.width(1)) register_1 (.D(decoder_1_out0), .clk(clock_2_out), .Q(OUTSEL));  // open: en, clr
  Clock clock_2 (.out(clock_2_out));
  assign RAM_ADDR = MEM_ADDRESS | MEM2_ADDRESS | LMEM_ADDRESS | LMEM2_ADDRESS;  // OR_Gate or_5, 8 bits wide
  assign RAM_OUT = MEM2_OUTPUT | MEM_OUTPUT;  // OR_Gate or_6, 8 bits wide
  and and_4 (CMPOT, cmp_1_equals, cmp2_1_equals);
  OUTB outb_1 (
    .ENABLE(OUTBI), .IDATA(IDATA), .REGISTER_A(AOUT), .REGISTER_B(BOUT), .REGISTER_C(COUT),
    .REGISTER_D(DOUT), .REGISTER_E(EOUT), .REGISTER_F(FOUT), .CPU_OUT(outb_1_cpu_out));
  INB inb_1 (.ENABLE(INBI), .IDATA(IDATA), .MAIN_IN(MAIN_INPUT), .REGS(INB_OUT), .UPDATE_REG(INB_UPDATE_REG));
  assign not_3_out = ~{8{OUTSEL}};  // NOT_Gate not_3, 8 bits wide
  assign MAIN_OUT = outb_1_cpu_out & not_3_out;  // AND_Gate and_5, 8 bits wide
  assign SECOND_OUT = outb_1_cpu_out & {8{OUTSEL}};  // AND_Gate and_6, 8 bits wide
  DEC dec_1 (
    .ENABLE(DECI), .IDATA(IDATA), .REGISTER_A(AOUT), .REGISTER_B(BOUT), .REGISTER_C(COUT), .REGISTER_D(DOUT),
    .REGISTER_E(EOUT), .REGISTER_F(FOUT), .EQUALS(DEC_EQUALS), .ERROR(DEC_ERROR), .UPDATE_REG(DEC_UPDATE_REG));
  JE je_1 (.CMP_OUT(CMPOT), .ENABLE(JEI), .IDATA(IDATA), .PM(PM_JE_OUT));
  assign or_7_out = INC_UPDATE_REG | INC2_UPDATE_REG | DEC_UPDATE_REG | DEC2_UPDATE_REG | SET_UPDATE_REG | INB_UPDATE_REG | LMEM_UPDATE | LMEM2_UPDATE;  // OR_Gate or_7, 4 bits wide
  Decoder #(.select(4)) decoder_2 (
    .out1(decoder_2_out1), .out2(decoder_2_out2), .out3(decoder_2_out3), .out4(decoder_2_out4),
    .out5(decoder_2_out5), .out6(decoder_2_out6), .sel(or_7_out));  // open: out0, out7, out8, out9, out10, out11, out12, out13, out14, out15, en
  DEC2 dec2_1 (
    .ENABLE(DEC2I), .IDATA(IDATA), .REGISTER_A(AOUT), .REGISTER_B(BOUT), .REGISTER_C(COUT),
    .REGISTER_D(DOUT), .REGISTER_E(EOUT), .REGISTER_F(FOUT), .EQUALS(DEC2_EQUALS), .ERROR(DEC2_ERROR),
    .UPDATE_REG(DEC2_UPDATE_REG));
  Register A (.D(or_8_out), .clk(decoder_2_out1), .Q(AOUT), .clr(RESET));  // open: en
  assign or_8_out = INC_EQUALS | INC2_EQUALS | DEC_EQUALS | DEC2_EQUALS | SET_OUT | INB_OUT | LMEM_OUTPUT | LMEM2_OUTPUT;  // OR_Gate or_8, 8 bits wide
  Register B (.D(or_9_out), .clk(decoder_2_out2), .Q(BOUT), .clr(RESET));  // open: en
  assign or_9_out = INC_EQUALS | INC2_EQUALS | DEC_EQUALS | DEC2_EQUALS | SET_OUT | INB_OUT | LMEM_OUTPUT | LMEM2_OUTPUT;  // OR_Gate or_9, 8 bits wide
  Register C (.D(or_10_out), .clk(decoder_2_out3), .Q(COUT), .clr(RESET));  // open: en
  assign or_10_out = INC_EQUALS | INC2_EQUALS | DEC_EQUALS | DEC2_EQUALS | SET_OUT | INB_OUT | LMEM_OUTPUT | LMEM2_OUTPUT;  // OR_Gate or_10, 8 bits wide
  Register D (.D(or_11_out), .clk(decoder_2_out4), .Q(DOUT), .clr(RESET));  // open: en
  assign or_11_out = INC_EQUALS | INC2_EQUALS | DEC_EQUALS | DEC2_EQUALS | SET_OUT | INB_OUT | LMEM_OUTPUT | LMEM2_OUTPUT;  // OR_Gate or_11, 8 bits wide
  Register E (.D(or_12_out), .clk(decoder_2_out5), .Q(EOUT), .clr(RESET));  // open: en
  assign or_12_out = INC_EQUALS | INC2_EQUALS | DEC_EQUALS | DEC2_EQUALS | SET_OUT | INB_OUT | LMEM_OUTPUT | LMEM2_OUTPUT;  // OR_Gate or_12, 8 bits wide
  Register F (.D(or_13_out), .clk(decoder_2_out6), .Q(FOUT), .clr(RESET));  // open: en
  assign or_13_out = INC_EQUALS | INC2_EQUALS | DEC_EQUALS | DEC2_EQUALS | SET_OUT | INB_OUT | LMEM_OUTPUT | LMEM2_OUTPUT;  // OR_Gate or_13, 8 bits wide
  SET set_1 (.ENABLE(SETI), .IDATA(IDATA), .REGS_OUT(SET_OUT), .UPDATE_REG(SET_UPDATE_REG));
  or or_14 (or_14_out, PM_JE_OUT[0], PM_JE_OUT[1]);
  or or_15 (or_15_out, PM_JE_OUT[2], PM_JE_OUT[3]);
  or or_16 (or_16_out, PM_JE_OUT[4], PM_JE_OUT[5]);
  or or_17 (or_17_out, PM_JE_OUT[6], PM_JE_OUT[7]);
  or or_18 (or_18_out, PM_JE_OUT[8], PM_JE_OUT[9]);
  or or_19 (or_19_out, PM_JE_OUT[10], PM_JE_OUT[11]);
  or or_20 (or_20_out, or_14_out, or_15_out);
  or or_21 (or_21_out, or_16_out, or_17_out);
  or or_22 (or_22_out, or_18_out, or_19_out);
  or or_23 (JE_PER, or_20_out, or_21_out, or_22_out);

  // Other names for the same wires on the sheet: RAM_OUT_t[7:0] = RAM_IN

  // Notes on the sheet:
  //   ARITHMETIC
  //   JUMP
  //   CLOCK
  //   MAIN
  //   RAM INSTRUCTIONS
  //   COMPARE
  //   I / O
  //   RAM
  //   REGS
  //   SET / MOV
endmodule

module INC (
  input  ENABLE,
  input  [11:0] IDATA,
  input  [7:0] REGISTER_A,
  input  [7:0] REGISTER_B,
  input  [7:0] REGISTER_C,
  input  [7:0] REGISTER_D,
  input  [7:0] REGISTER_E,
  input  [7:0] REGISTER_F,
  output [7:0] EQUALS,
  output ERROR,
  output [3:0] UPDATE_REG
);

  wire clock_1_out;
  wire [3:0] and_1_out;
  wire [3:3] not_1_out;
  wire [7:0] and_1_out_2, and_2_out, and_3_out, and_4_out, and_5_out, and_6_out, and_7_out, and_8_out,
       and_9_out, and_10_out, and_11_out, and_12_out, and_13_out, or_1_out, or_2_out;
  wire [7:7] decoder_1_out1, decoder_1_out2, decoder_1_out3, decoder_1_out4, decoder_1_out5, decoder_1_out6,
       decoder_2_out1, decoder_2_out2, decoder_2_out3, decoder_2_out4, decoder_2_out5, decoder_2_out6;

  Decoder #(.select(4)) decoder_1 (
    .out1(decoder_1_out1[7]), .out2(decoder_1_out2[7]), .out3(decoder_1_out3[7]), .out4(decoder_1_out4[7]),
    .out5(decoder_1_out5[7]), .out6(decoder_1_out6[7]), .sel(and_1_out));  // open: out0, out7, out8, out9, out10, out11, out12, out13, out14, out15, en
  Decoder #(.select(4)) decoder_2 (
    .out1(decoder_2_out1[7]), .out2(decoder_2_out2[7]), .out3(decoder_2_out3[7]), .out4(decoder_2_out4[7]),
    .out5(decoder_2_out5[7]), .out6(decoder_2_out6[7]), .sel(and_1_out_2[7:4]));  // open: out0, out7, out8, out9, out10, out11, out12, out13, out14, out15, en
  assign {and_1_out, and_1_out_2} = {12{ENABLE}} & IDATA;  // AND_Gate and_1, 12 bits wide
  assign and_2_out = {8{decoder_1_out1[7]}} & REGISTER_A;  // AND_Gate and_2, 8 bits wide
  assign and_3_out = {8{decoder_1_out2[7]}} & REGISTER_B;  // AND_Gate and_3, 8 bits wide
  assign and_4_out = {8{decoder_1_out3[7]}} & REGISTER_C;  // AND_Gate and_4, 8 bits wide
  assign and_5_out = {8{decoder_1_out4[7]}} & REGISTER_D;  // AND_Gate and_5, 8 bits wide
  assign and_6_out = {8{decoder_1_out5[7]}} & REGISTER_E;  // AND_Gate and_6, 8 bits wide
  assign and_7_out = {8{decoder_1_out6[7]}} & REGISTER_F;  // AND_Gate and_7, 8 bits wide
  assign and_8_out = {8{decoder_2_out1[7]}} & REGISTER_A;  // AND_Gate and_8, 8 bits wide
  assign and_9_out = {8{decoder_2_out2[7]}} & REGISTER_B;  // AND_Gate and_9, 8 bits wide
  assign and_10_out = {8{decoder_2_out3[7]}} & REGISTER_C;  // AND_Gate and_10, 8 bits wide
  assign and_11_out = {8{decoder_2_out4[7]}} & REGISTER_D;  // AND_Gate and_11, 8 bits wide
  assign and_12_out = {8{decoder_2_out5[7]}} & REGISTER_E;  // AND_Gate and_12, 8 bits wide
  assign and_13_out = {8{decoder_2_out6[7]}} & REGISTER_F;  // AND_Gate and_13, 8 bits wide
  Clock clock_1 (.out(clock_1_out));
  assign or_1_out = and_2_out | and_7_out | and_3_out | and_4_out | and_5_out | and_6_out;  // OR_Gate or_1, 8 bits wide
  assign or_2_out = and_8_out | and_9_out | and_10_out | and_11_out | and_12_out | and_13_out;  // OR_Gate or_2, 8 bits wide
  not not_1 (not_1_out[3], clock_1_out);
  assign UPDATE_REG = {4{not_1_out[3]}} & and_1_out;  // AND_Gate and_14, 4 bits wide
  Adder adder_1 (.a(or_1_out), .b(or_2_out), .out(EQUALS), .cout(ERROR));  // open: cin
endmodule

module INC2 (
  input  ENABLE,
  input  [11:0] IDATA,
  input  [7:0] REGISTER_A,
  input  [7:0] REGISTER_B,
  input  [7:0] REGISTER_C,
  input  [7:0] REGISTER_D,
  input  [7:0] REGISTER_E,
  input  [7:0] REGISTER_F,
  output [7:0] EQUALS,
  output ERROR,
  output [3:0] UPDATE_REG
);

  wire clock_1_out;
  wire [3:0] and_1_out;
  wire [3:3] not_1_out;
  wire [7:0] and_1_out_2, and_2_out, and_3_out, and_4_out, and_5_out, and_6_out, and_7_out, or_1_out;
  wire [7:7] decoder_1_out1, decoder_1_out2, decoder_1_out3, decoder_1_out4, decoder_1_out5, decoder_1_out6;

  Decoder #(.select(4)) decoder_1 (
    .out1(decoder_1_out1[7]), .out2(decoder_1_out2[7]), .out3(decoder_1_out3[7]), .out4(decoder_1_out4[7]),
    .out5(decoder_1_out5[7]), .out6(decoder_1_out6[7]), .sel(and_1_out));  // open: out0, out7, out8, out9, out10, out11, out12, out13, out14, out15, en
  assign {and_1_out, and_1_out_2} = {12{ENABLE}} & IDATA;  // AND_Gate and_1, 12 bits wide
  assign and_2_out = {8{decoder_1_out1[7]}} & REGISTER_A;  // AND_Gate and_2, 8 bits wide
  assign and_3_out = {8{decoder_1_out2[7]}} & REGISTER_B;  // AND_Gate and_3, 8 bits wide
  assign and_4_out = {8{decoder_1_out3[7]}} & REGISTER_C;  // AND_Gate and_4, 8 bits wide
  assign and_5_out = {8{decoder_1_out4[7]}} & REGISTER_D;  // AND_Gate and_5, 8 bits wide
  assign and_6_out = {8{decoder_1_out5[7]}} & REGISTER_E;  // AND_Gate and_6, 8 bits wide
  assign and_7_out = {8{decoder_1_out6[7]}} & REGISTER_F;  // AND_Gate and_7, 8 bits wide
  Clock clock_1 (.out(clock_1_out));
  assign or_1_out = and_2_out | and_7_out | and_3_out | and_4_out | and_5_out | and_6_out;  // OR_Gate or_1, 8 bits wide
  not not_1 (not_1_out[3], clock_1_out);
  assign UPDATE_REG = {4{not_1_out[3]}} & and_1_out;  // AND_Gate and_8, 4 bits wide
  Adder adder_1 (.a(or_1_out), .b(and_1_out_2), .out(EQUALS), .cout(ERROR));  // open: cin
endmodule

module DEC (
  input  ENABLE,
  input  [11:0] IDATA,
  input  [7:0] REGISTER_A,
  input  [7:0] REGISTER_B,
  input  [7:0] REGISTER_C,
  input  [7:0] REGISTER_D,
  input  [7:0] REGISTER_E,
  input  [7:0] REGISTER_F,
  output [7:0] EQUALS,
  output ERROR,
  output [3:0] UPDATE_REG
);

  wire clock_1_out;
  wire [3:0] and_1_out;
  wire [3:3] not_1_out;
  wire [7:0] and_1_out_2, and_2_out, and_3_out, and_4_out, and_5_out, and_6_out, and_7_out, and_8_out,
       and_9_out, and_10_out, and_11_out, and_12_out, and_13_out, or_1_out, or_2_out;
  wire [7:7] decoder_1_out1, decoder_1_out2, decoder_1_out3, decoder_1_out4, decoder_1_out5, decoder_1_out6,
       decoder_2_out1, decoder_2_out2, decoder_2_out3, decoder_2_out4, decoder_2_out5, decoder_2_out6;

  Decoder #(.select(4)) decoder_1 (
    .out1(decoder_1_out1[7]), .out2(decoder_1_out2[7]), .out3(decoder_1_out3[7]), .out4(decoder_1_out4[7]),
    .out5(decoder_1_out5[7]), .out6(decoder_1_out6[7]), .sel(and_1_out));  // open: out0, out7, out8, out9, out10, out11, out12, out13, out14, out15, en
  Decoder #(.select(4)) decoder_2 (
    .out1(decoder_2_out1[7]), .out2(decoder_2_out2[7]), .out3(decoder_2_out3[7]), .out4(decoder_2_out4[7]),
    .out5(decoder_2_out5[7]), .out6(decoder_2_out6[7]), .sel(and_1_out_2[7:4]));  // open: out0, out7, out8, out9, out10, out11, out12, out13, out14, out15, en
  assign {and_1_out, and_1_out_2} = {12{ENABLE}} & IDATA;  // AND_Gate and_1, 12 bits wide
  assign and_2_out = {8{decoder_1_out1[7]}} & REGISTER_A;  // AND_Gate and_2, 8 bits wide
  assign and_3_out = {8{decoder_1_out2[7]}} & REGISTER_B;  // AND_Gate and_3, 8 bits wide
  assign and_4_out = {8{decoder_1_out3[7]}} & REGISTER_C;  // AND_Gate and_4, 8 bits wide
  assign and_5_out = {8{decoder_1_out4[7]}} & REGISTER_D;  // AND_Gate and_5, 8 bits wide
  assign and_6_out = {8{decoder_1_out5[7]}} & REGISTER_E;  // AND_Gate and_6, 8 bits wide
  assign and_7_out = {8{decoder_1_out6[7]}} & REGISTER_F;  // AND_Gate and_7, 8 bits wide
  assign and_8_out = {8{decoder_2_out1[7]}} & REGISTER_A;  // AND_Gate and_8, 8 bits wide
  assign and_9_out = {8{decoder_2_out2[7]}} & REGISTER_B;  // AND_Gate and_9, 8 bits wide
  assign and_10_out = {8{decoder_2_out3[7]}} & REGISTER_C;  // AND_Gate and_10, 8 bits wide
  assign and_11_out = {8{decoder_2_out4[7]}} & REGISTER_D;  // AND_Gate and_11, 8 bits wide
  assign and_12_out = {8{decoder_2_out5[7]}} & REGISTER_E;  // AND_Gate and_12, 8 bits wide
  assign and_13_out = {8{decoder_2_out6[7]}} & REGISTER_F;  // AND_Gate and_13, 8 bits wide
  Clock clock_1 (.out(clock_1_out));
  assign or_1_out = and_2_out | and_7_out | and_3_out | and_4_out | and_5_out | and_6_out;  // OR_Gate or_1, 8 bits wide
  assign or_2_out = and_8_out | and_9_out | and_10_out | and_11_out | and_12_out | and_13_out;  // OR_Gate or_2, 8 bits wide
  not not_1 (not_1_out[3], clock_1_out);
  assign UPDATE_REG = {4{not_1_out[3]}} & and_1_out;  // AND_Gate and_14, 4 bits wide
  Subtractor subtractor_1 (.a(or_1_out), .b(or_2_out), .out(EQUALS), .bout(ERROR));  // open: bin
endmodule

module DEC2 (
  input  ENABLE,
  input  [11:0] IDATA,
  input  [7:0] REGISTER_A,
  input  [7:0] REGISTER_B,
  input  [7:0] REGISTER_C,
  input  [7:0] REGISTER_D,
  input  [7:0] REGISTER_E,
  input  [7:0] REGISTER_F,
  output [7:0] EQUALS,
  output ERROR,
  output [3:0] UPDATE_REG
);

  wire clock_1_out;
  wire [3:0] and_1_out;
  wire [3:3] not_1_out;
  wire [7:0] and_1_out_2, and_2_out, and_3_out, and_4_out, and_5_out, and_6_out, and_7_out, or_1_out;
  wire [7:7] decoder_1_out1, decoder_1_out2, decoder_1_out3, decoder_1_out4, decoder_1_out5, decoder_1_out6;

  Decoder #(.select(4)) decoder_1 (
    .out1(decoder_1_out1[7]), .out2(decoder_1_out2[7]), .out3(decoder_1_out3[7]), .out4(decoder_1_out4[7]),
    .out5(decoder_1_out5[7]), .out6(decoder_1_out6[7]), .sel(and_1_out));  // open: out0, out7, out8, out9, out10, out11, out12, out13, out14, out15, en
  assign {and_1_out, and_1_out_2} = {12{ENABLE}} & IDATA;  // AND_Gate and_1, 12 bits wide
  assign and_2_out = {8{decoder_1_out1[7]}} & REGISTER_A;  // AND_Gate and_2, 8 bits wide
  assign and_3_out = {8{decoder_1_out2[7]}} & REGISTER_B;  // AND_Gate and_3, 8 bits wide
  assign and_4_out = {8{decoder_1_out3[7]}} & REGISTER_C;  // AND_Gate and_4, 8 bits wide
  assign and_5_out = {8{decoder_1_out4[7]}} & REGISTER_D;  // AND_Gate and_5, 8 bits wide
  assign and_6_out = {8{decoder_1_out5[7]}} & REGISTER_E;  // AND_Gate and_6, 8 bits wide
  assign and_7_out = {8{decoder_1_out6[7]}} & REGISTER_F;  // AND_Gate and_7, 8 bits wide
  Clock clock_1 (.out(clock_1_out));
  assign or_1_out = and_2_out | and_7_out | and_3_out | and_4_out | and_5_out | and_6_out;  // OR_Gate or_1, 8 bits wide
  not not_1 (not_1_out[3], clock_1_out);
  assign UPDATE_REG = {4{not_1_out[3]}} & and_1_out;  // AND_Gate and_8, 4 bits wide
  Subtractor subtractor_1 (.a(or_1_out), .b(and_1_out_2), .out(EQUALS), .bout(ERROR));  // open: bin
endmodule

module JMP (
  input  ENABLE,
  input  [11:0] IDATA,
  output [11:0] PM
);

  and and_1 (PM[11], IDATA[11], ENABLE);
  and and_2 (PM[10], IDATA[10], ENABLE);
  and and_3 (PM[9], IDATA[9], ENABLE);
  and and_4 (PM[8], IDATA[8], ENABLE);
  and and_5 (PM[7], IDATA[7], ENABLE);
  and and_6 (PM[6], IDATA[6], ENABLE);
  and and_7 (PM[5], IDATA[5], ENABLE);
  and and_8 (PM[4], IDATA[4], ENABLE);
  and and_9 (PM[3], IDATA[3], ENABLE);
  and and_10 (PM[2], IDATA[2], ENABLE);
  and and_11 (PM[1], IDATA[1], ENABLE);
  and and_12 (PM[0], IDATA[0], ENABLE);
endmodule

module CMP (
  input  ENABLE,
  input  [11:0] IDATA,
  input  [7:0] REGISTER_A,
  input  [7:0] REGISTER_B,
  input  [7:0] REGISTER_C,
  input  [7:0] REGISTER_D,
  input  [7:0] REGISTER_E,
  input  [7:0] REGISTER_F,
  output EQUALS
);

  wire and_14_out, clock_1_out, xor_1_out, xor_2_out, xor_3_out, xor_4_out, xor_5_out, xor_6_out, xor_7_out,
       xor_8_out;
  wire [7:0] and_2_out, and_3_out, and_4_out, and_5_out, and_6_out, and_7_out, and_8_out, and_9_out,
       and_10_out, and_11_out, and_12_out, and_13_out, or_1_out, or_2_out;
  wire [7:7] decoder_1_out1, decoder_1_out2, decoder_1_out3, decoder_1_out4, decoder_1_out5, decoder_1_out6,
       decoder_2_out1, decoder_2_out2, decoder_2_out3, decoder_2_out4, decoder_2_out5, decoder_2_out6;
  wire [11:0] and_1_out;

  Decoder #(.select(4)) decoder_1 (
    .out1(decoder_1_out1[7]), .out2(decoder_1_out2[7]), .out3(decoder_1_out3[7]), .out4(decoder_1_out4[7]),
    .out5(decoder_1_out5[7]), .out6(decoder_1_out6[7]), .sel(and_1_out[11:8]));  // open: out0, out7, out8, out9, out10, out11, out12, out13, out14, out15, en
  Decoder #(.select(4)) decoder_2 (
    .out1(decoder_2_out1[7]), .out2(decoder_2_out2[7]), .out3(decoder_2_out3[7]), .out4(decoder_2_out4[7]),
    .out5(decoder_2_out5[7]), .out6(decoder_2_out6[7]), .sel(and_1_out[7:4]));  // open: out0, out7, out8, out9, out10, out11, out12, out13, out14, out15, en
  assign and_1_out = {12{ENABLE}} & IDATA;  // AND_Gate and_1, 12 bits wide
  assign and_2_out = {8{decoder_1_out1[7]}} & REGISTER_A;  // AND_Gate and_2, 8 bits wide
  assign and_3_out = {8{decoder_1_out2[7]}} & REGISTER_B;  // AND_Gate and_3, 8 bits wide
  assign and_4_out = {8{decoder_1_out3[7]}} & REGISTER_C;  // AND_Gate and_4, 8 bits wide
  assign and_5_out = {8{decoder_1_out4[7]}} & REGISTER_D;  // AND_Gate and_5, 8 bits wide
  assign and_6_out = {8{decoder_1_out5[7]}} & REGISTER_E;  // AND_Gate and_6, 8 bits wide
  assign and_7_out = {8{decoder_1_out6[7]}} & REGISTER_F;  // AND_Gate and_7, 8 bits wide
  assign and_8_out = {8{decoder_2_out1[7]}} & REGISTER_A;  // AND_Gate and_8, 8 bits wide
  assign and_9_out = {8{decoder_2_out2[7]}} & REGISTER_B;  // AND_Gate and_9, 8 bits wide
  assign and_10_out = {8{decoder_2_out3[7]}} & REGISTER_C;  // AND_Gate and_10, 8 bits wide
  assign and_11_out = {8{decoder_2_out4[7]}} & REGISTER_D;  // AND_Gate and_11, 8 bits wide
  assign and_12_out = {8{decoder_2_out5[7]}} & REGISTER_E;  // AND_Gate and_12, 8 bits wide
  assign and_13_out = {8{decoder_2_out6[7]}} & REGISTER_F;  // AND_Gate and_13, 8 bits wide
  assign or_1_out = and_2_out | and_7_out | and_3_out | and_4_out | and_5_out | and_6_out;  // OR_Gate or_1, 8 bits wide
  assign or_2_out = and_8_out | and_9_out | and_10_out | and_11_out | and_12_out | and_13_out;  // OR_Gate or_2, 8 bits wide
  xor xor_1 (xor_1_out, or_1_out[7], or_2_out[7]);
  xor xor_2 (xor_2_out, or_1_out[5], or_2_out[5]);
  xor xor_3 (xor_3_out, or_1_out[6], or_2_out[6]);
  xor xor_4 (xor_4_out, or_1_out[3], or_2_out[3]);
  xor xor_5 (xor_5_out, or_1_out[4], or_2_out[4]);
  xor xor_6 (xor_6_out, or_1_out[2], or_2_out[2]);
  xor xor_7 (xor_7_out, or_1_out[0], or_2_out[0]);
  xor xor_8 (xor_8_out, or_1_out[1], or_2_out[1]);
  Register #(.width(1)) register_1 (.D(and_14_out), .clk(clock_1_out), .Q(EQUALS));  // open: en, clr
  and and_14 (and_14_out, ~xor_7_out, ~xor_8_out, ~xor_6_out, ~xor_4_out, ~xor_5_out, ~xor_2_out, ~xor_3_out, ~xor_1_out);  // AND_Gate
  Clock clock_1 (.out(clock_1_out));
endmodule

module CMP2 (
  input  ENABLE,
  input  [11:0] IDATA,
  input  [7:0] REGISTER_A,
  input  [7:0] REGISTER_B,
  input  [7:0] REGISTER_C,
  input  [7:0] REGISTER_D,
  input  [7:0] REGISTER_E,
  input  [7:0] REGISTER_F,
  output EQUALS
);

  wire and_8_out, clock_1_out, xor_1_out, xor_2_out, xor_3_out, xor_4_out, xor_5_out, xor_6_out, xor_7_out,
       xor_8_out;
  wire [7:0] and_2_out, and_3_out, and_4_out, and_5_out, and_6_out, and_7_out, or_1_out;
  wire [7:7] decoder_1_out1, decoder_1_out2, decoder_1_out3, decoder_1_out4, decoder_1_out5, decoder_1_out6;
  wire [11:0] and_1_out;

  Decoder #(.select(4)) decoder_1 (
    .out1(decoder_1_out1[7]), .out2(decoder_1_out2[7]), .out3(decoder_1_out3[7]), .out4(decoder_1_out4[7]),
    .out5(decoder_1_out5[7]), .out6(decoder_1_out6[7]), .sel(and_1_out[11:8]));  // open: out0, out7, out8, out9, out10, out11, out12, out13, out14, out15, en
  assign and_1_out = {12{ENABLE}} & IDATA;  // AND_Gate and_1, 12 bits wide
  assign and_2_out = {8{decoder_1_out1[7]}} & REGISTER_A;  // AND_Gate and_2, 8 bits wide
  assign and_3_out = {8{decoder_1_out2[7]}} & REGISTER_B;  // AND_Gate and_3, 8 bits wide
  assign and_4_out = {8{decoder_1_out3[7]}} & REGISTER_C;  // AND_Gate and_4, 8 bits wide
  assign and_5_out = {8{decoder_1_out4[7]}} & REGISTER_D;  // AND_Gate and_5, 8 bits wide
  assign and_6_out = {8{decoder_1_out5[7]}} & REGISTER_E;  // AND_Gate and_6, 8 bits wide
  assign and_7_out = {8{decoder_1_out6[7]}} & REGISTER_F;  // AND_Gate and_7, 8 bits wide
  assign or_1_out = and_2_out | and_7_out | and_3_out | and_4_out | and_5_out | and_6_out;  // OR_Gate or_1, 8 bits wide
  xor xor_1 (xor_1_out, or_1_out[7], and_1_out[7]);
  xor xor_2 (xor_2_out, or_1_out[5], and_1_out[5]);
  xor xor_3 (xor_3_out, or_1_out[6], and_1_out[6]);
  xor xor_4 (xor_4_out, or_1_out[3], and_1_out[3]);
  xor xor_5 (xor_5_out, or_1_out[4], and_1_out[4]);
  xor xor_6 (xor_6_out, or_1_out[2], and_1_out[2]);
  xor xor_7 (xor_7_out, or_1_out[0], and_1_out[0]);
  xor xor_8 (xor_8_out, or_1_out[1], and_1_out[1]);
  Register #(.width(1)) register_1 (.D(and_8_out), .clk(clock_1_out), .Q(EQUALS));  // open: en, clr
  and and_8 (and_8_out, ~xor_7_out, ~xor_8_out, ~xor_6_out, ~xor_4_out, ~xor_5_out, ~xor_2_out, ~xor_3_out, ~xor_1_out);  // AND_Gate
  Clock clock_1 (.out(clock_1_out));
endmodule

module JE (
  input  CMP_OUT,
  input  ENABLE,
  input  [11:0] IDATA,
  output [11:0] PM
);

  wire and_1_out;

  and and_1 (and_1_out, ENABLE, CMP_OUT);
  and and_2 (PM[11], IDATA[11], and_1_out);
  and and_3 (PM[10], IDATA[10], and_1_out);
  and and_4 (PM[9], IDATA[9], and_1_out);
  and and_5 (PM[8], IDATA[8], and_1_out);
  and and_6 (PM[7], IDATA[7], and_1_out);
  and and_7 (PM[6], IDATA[6], and_1_out);
  and and_8 (PM[5], IDATA[5], and_1_out);
  and and_9 (PM[4], IDATA[4], and_1_out);
  and and_10 (PM[3], IDATA[3], and_1_out);
  and and_11 (PM[2], IDATA[2], and_1_out);
  and and_12 (PM[1], IDATA[1], and_1_out);
  and and_13 (PM[0], IDATA[0], and_1_out);
endmodule

module SET (
  input  ENABLE,
  input  [11:0] IDATA,
  output [7:0] REGS_OUT,
  output [3:0] UPDATE_REG
);

  wire [3:3] clock_1_out;
  wire [11:8] and_1_out;

  assign {and_1_out, REGS_OUT} = {12{ENABLE}} & IDATA;  // AND_Gate and_1, 12 bits wide
  Clock clock_1 (.out(clock_1_out[3]));
  assign UPDATE_REG = {4{clock_1_out[3]}} & and_1_out;  // AND_Gate and_2, 4 bits wide
endmodule

module OUTB (
  input  ENABLE,
  input  [11:0] IDATA,
  input  [7:0] REGISTER_A,
  input  [7:0] REGISTER_B,
  input  [7:0] REGISTER_C,
  input  [7:0] REGISTER_D,
  input  [7:0] REGISTER_E,
  input  [7:0] REGISTER_F,
  output [7:0] CPU_OUT
);

  wire [7:0] and_2_out, and_3_out, and_4_out, and_5_out, and_6_out, and_7_out;
  wire [7:7] decoder_1_out1, decoder_1_out2, decoder_1_out3, decoder_1_out4, decoder_1_out5, decoder_1_out6;
  wire [11:0] and_1_out;

  Decoder #(.select(4)) decoder_1 (
    .out1(decoder_1_out1[7]), .out2(decoder_1_out2[7]), .out3(decoder_1_out3[7]), .out4(decoder_1_out4[7]),
    .out5(decoder_1_out5[7]), .out6(decoder_1_out6[7]), .sel(and_1_out[11:8]));  // open: out0, out7, out8, out9, out10, out11, out12, out13, out14, out15, en
  assign and_1_out = {12{ENABLE}} & IDATA;  // AND_Gate and_1, 12 bits wide
  assign and_2_out = {8{decoder_1_out1[7]}} & REGISTER_A;  // AND_Gate and_2, 8 bits wide
  assign and_3_out = {8{decoder_1_out2[7]}} & REGISTER_B;  // AND_Gate and_3, 8 bits wide
  assign and_4_out = {8{decoder_1_out3[7]}} & REGISTER_C;  // AND_Gate and_4, 8 bits wide
  assign and_5_out = {8{decoder_1_out4[7]}} & REGISTER_D;  // AND_Gate and_5, 8 bits wide
  assign and_6_out = {8{decoder_1_out5[7]}} & REGISTER_E;  // AND_Gate and_6, 8 bits wide
  assign and_7_out = {8{decoder_1_out6[7]}} & REGISTER_F;  // AND_Gate and_7, 8 bits wide
  assign CPU_OUT = and_2_out | and_7_out | and_3_out | and_4_out | and_5_out | and_6_out;  // OR_Gate or_1, 8 bits wide
endmodule

module INB (
  input  ENABLE,
  input  [11:0] IDATA,
  input  [7:0] MAIN_IN,
  output [7:0] REGS,
  output [3:0] UPDATE_REG
);

  wire [3:3] clock_1_out;
  wire [11:0] and_1_out;

  assign and_1_out = {12{ENABLE}} & IDATA;  // AND_Gate and_1, 12 bits wide
  assign REGS = {8{ENABLE}} & MAIN_IN;  // AND_Gate and_2, 8 bits wide
  Clock clock_1 (.out(clock_1_out[3]));
  assign UPDATE_REG = {4{clock_1_out[3]}} & and_1_out[11:8];  // AND_Gate and_3, 4 bits wide
endmodule

module MEM (
  input  ENABLE,
  input  [11:0] IDATA,
  input  [7:0] REGISTER_A,
  input  [7:0] REGISTER_B,
  input  [7:0] REGISTER_C,
  input  [7:0] REGISTER_D,
  input  [7:0] REGISTER_E,
  input  [7:0] REGISTER_F,
  output [7:0] RAM_ADDRESS,
  output [7:0] EQUALS,
  output UPDATE_RAM
);

  wire clock_1_out;
  wire [7:0] and_2_out, and_3_out, and_4_out, and_5_out, and_6_out, and_7_out;
  wire [7:7] decoder_1_out1, decoder_1_out2, decoder_1_out3, decoder_1_out4, decoder_1_out5, decoder_1_out6;
  wire [11:8] and_1_out;

  Decoder #(.select(4)) decoder_1 (
    .out1(decoder_1_out1[7]), .out2(decoder_1_out2[7]), .out3(decoder_1_out3[7]), .out4(decoder_1_out4[7]),
    .out5(decoder_1_out5[7]), .out6(decoder_1_out6[7]), .sel(and_1_out));  // open: out0, out7, out8, out9, out10, out11, out12, out13, out14, out15, en
  assign {and_1_out, RAM_ADDRESS} = {12{ENABLE}} & IDATA;  // AND_Gate and_1, 12 bits wide
  assign and_2_out = {8{decoder_1_out1[7]}} & REGISTER_A;  // AND_Gate and_2, 8 bits wide
  assign and_3_out = {8{decoder_1_out2[7]}} & REGISTER_B;  // AND_Gate and_3, 8 bits wide
  assign and_4_out = {8{decoder_1_out3[7]}} & REGISTER_C;  // AND_Gate and_4, 8 bits wide
  assign and_5_out = {8{decoder_1_out4[7]}} & REGISTER_D;  // AND_Gate and_5, 8 bits wide
  assign and_6_out = {8{decoder_1_out5[7]}} & REGISTER_E;  // AND_Gate and_6, 8 bits wide
  assign and_7_out = {8{decoder_1_out6[7]}} & REGISTER_F;  // AND_Gate and_7, 8 bits wide
  assign EQUALS = and_2_out | and_7_out | and_3_out | and_4_out | and_5_out | and_6_out;  // OR_Gate or_1, 8 bits wide
  Clock clock_1 (.out(clock_1_out));
  and and_8 (UPDATE_RAM, clock_1_out, ENABLE);
endmodule

module MEM2 (
  input  ENABLE,
  input  [11:0] IDATA,
  input  [7:0] REGISTER_A,
  input  [7:0] REGISTER_B,
  input  [7:0] REGISTER_C,
  input  [7:0] REGISTER_D,
  input  [7:0] REGISTER_E,
  input  [7:0] REGISTER_F,
  output [7:0] MEM_OUT,
  output [7:0] MEM_ADDRESS,
  output UPDATE_RAM
);

  wire clock_1_out;
  wire [3:0] and_1_out;
  wire [7:0] and_1_out_2, and_2_out, and_3_out, and_4_out, and_5_out, and_6_out, and_7_out, and_8_out,
       and_9_out, and_10_out, and_11_out, and_12_out, and_13_out;
  wire [7:7] decoder_1_out1, decoder_1_out2, decoder_1_out3, decoder_1_out4, decoder_1_out5, decoder_1_out6,
       decoder_2_out1, decoder_2_out2, decoder_2_out3, decoder_2_out4, decoder_2_out5, decoder_2_out6;

  Decoder #(.select(4)) decoder_1 (
    .out1(decoder_1_out1[7]), .out2(decoder_1_out2[7]), .out3(decoder_1_out3[7]), .out4(decoder_1_out4[7]),
    .out5(decoder_1_out5[7]), .out6(decoder_1_out6[7]), .sel(and_1_out_2[7:4]));  // open: out0, out7, out8, out9, out10, out11, out12, out13, out14, out15, en
  Decoder #(.select(4)) decoder_2 (
    .out1(decoder_2_out1[7]), .out2(decoder_2_out2[7]), .out3(decoder_2_out3[7]), .out4(decoder_2_out4[7]),
    .out5(decoder_2_out5[7]), .out6(decoder_2_out6[7]), .sel(and_1_out));  // open: out0, out7, out8, out9, out10, out11, out12, out13, out14, out15, en
  assign {and_1_out, and_1_out_2} = {12{ENABLE}} & IDATA;  // AND_Gate and_1, 12 bits wide
  assign and_2_out = {8{decoder_1_out1[7]}} & REGISTER_A;  // AND_Gate and_2, 8 bits wide
  assign and_3_out = {8{decoder_1_out2[7]}} & REGISTER_B;  // AND_Gate and_3, 8 bits wide
  assign and_4_out = {8{decoder_1_out3[7]}} & REGISTER_C;  // AND_Gate and_4, 8 bits wide
  assign and_5_out = {8{decoder_1_out4[7]}} & REGISTER_D;  // AND_Gate and_5, 8 bits wide
  assign and_6_out = {8{decoder_1_out5[7]}} & REGISTER_E;  // AND_Gate and_6, 8 bits wide
  assign and_7_out = {8{decoder_1_out6[7]}} & REGISTER_F;  // AND_Gate and_7, 8 bits wide
  assign and_8_out = {8{decoder_2_out1[7]}} & REGISTER_A;  // AND_Gate and_8, 8 bits wide
  assign and_9_out = {8{decoder_2_out2[7]}} & REGISTER_B;  // AND_Gate and_9, 8 bits wide
  assign and_10_out = {8{decoder_2_out3[7]}} & REGISTER_C;  // AND_Gate and_10, 8 bits wide
  assign and_11_out = {8{decoder_2_out4[7]}} & REGISTER_D;  // AND_Gate and_11, 8 bits wide
  assign and_12_out = {8{decoder_2_out5[7]}} & REGISTER_E;  // AND_Gate and_12, 8 bits wide
  assign and_13_out = {8{decoder_2_out6[7]}} & REGISTER_F;  // AND_Gate and_13, 8 bits wide
  assign MEM_OUT = and_2_out | and_7_out | and_3_out | and_4_out | and_5_out | and_6_out;  // OR_Gate or_1, 8 bits wide
  assign MEM_ADDRESS = and_8_out | and_9_out | and_10_out | and_11_out | and_12_out | and_13_out;  // OR_Gate or_2, 8 bits wide
  Clock clock_1 (.out(clock_1_out));
  and and_14 (UPDATE_RAM, clock_1_out, ENABLE);
endmodule

module LMEM (
  input  ENABLE,
  input  [11:0] IDATA,
  input  [7:0] RAM,
  output [7:0] RAM_ADDRESS,
  output [7:0] RAM_OUT,
  output [3:0] UPDATE_REG
);

  wire [3:3] clock_1_out;
  wire [11:8] and_1_out;

  assign {and_1_out, RAM_ADDRESS} = {12{ENABLE}} & IDATA;  // AND_Gate and_1, 12 bits wide
  Clock clock_1 (.out(clock_1_out[3]));
  assign UPDATE_REG = {4{clock_1_out[3]}} & and_1_out;  // AND_Gate and_2, 4 bits wide

  assign RAM_OUT = RAM;
endmodule

module LMEM2 (
  input  ENABLE,
  input  [11:0] IDATA,
  input  [7:0] A,
  input  [7:0] B,
  input  [7:0] C,
  input  [7:0] D,
  input  [7:0] E,
  input  [7:0] F,
  input  [7:0] RAM,
  output [7:0] RAM_ADDRESS,
  output [7:0] RAM_OUT,
  output [3:0] UPDATE_REG
);

  wire [3:3] clock_1_out;
  wire [11:0] and_1_out;

  assign and_1_out = {12{ENABLE}} & IDATA;  // AND_Gate and_1, 12 bits wide
  Multiplexer #(.select(4), .width(8)) multiplexer_1 (
    .in0({8{1'b0}}), .in1(A), .in2(B), .in3(C), .in4(D), .in5(E), .in6(F), .out(RAM_ADDRESS),
    .sel(and_1_out[7:4]));  // open: in7, in8, in9, in10, in11, in12, in13, in14, in15
  Clock clock_1 (.out(clock_1_out[3]));
  assign UPDATE_REG = {4{clock_1_out[3]}} & and_1_out[11:8];  // AND_Gate and_2, 4 bits wide

  assign RAM_OUT = RAM;
endmodule
