// Logisim project PC.circ as structural Verilog: 2 circuits, main circuit Computer
module Desk (
  input  in_1
);

  wire switch_1_p2;

  // Switch switch_1: pin names not known; wires that end beside it: in_1, switch_1_p2
  Computer computer_1 (.in_1(switch_1_p2));  // open: in_2
endmodule

module Computer (
  input  in_1,
  input  [7:0] in_2
);

  wire clock_1_out, cpu_1_ram_clk, cpu_1_ram_we, not_1_out;
  wire [3:0] cpu_1_main_out, cpu_1_main_out_2;
  wire [7:0] cpu_1_ram_addr, cpu_1_ram_out, ram_1_dout;
  wire [11:0] cpu_1_rom_addr;
  wire [15:0] rom_1_data;

  ROM #(.addrWidth(12), .dataWidth(16)) rom_1 (.addr(cpu_1_rom_addr), .data(rom_1_data));
  LED POWER (.in(in_1));
  not not_1 (not_1_out, in_1);
  CPU cpu_1 (
    .RAM_IN(ram_1_dout), .ENABLE(in_1), .MAIN_INPUT(in_2), .RESET(not_1_out), .ROM_DATA(rom_1_data),
    .ROM_ADDR(cpu_1_rom_addr), .MAIN_OUT({cpu_1_main_out, cpu_1_main_out_2}), .RAM_ADDR(cpu_1_ram_addr),
    .RAM_WE(cpu_1_ram_we), .RAM_CLK(cpu_1_ram_clk), .RAM_OUT(cpu_1_ram_out));
  RAM #(.enables("line")) ram_1 (
    .addr(cpu_1_ram_addr), .we(cpu_1_ram_we), .clk(cpu_1_ram_clk), .din(cpu_1_ram_out), .dout(ram_1_dout));
  Hex_Digit_Display hex_digit_display_1 (.value(cpu_1_main_out));  // open: dp
  Hex_Digit_Display hex_digit_display_2 (.value(cpu_1_main_out_2));  // open: dp
  Clock clock_1 (.out(clock_1_out));
  TTY #(.rows(16)) tty_1 (
    .data({cpu_1_main_out[2:0], cpu_1_main_out_2}), .clk(clock_1_out), .clr(not_1_out));  // open: we
endmodule
